// Logisim project mini_chip8_alu3.circ as structural Verilog: 8 circuits, main circuit ALU3
module ALU3 (
  input  [3:0] Y,
  input  [3:0] X,
  input  [7:0] VX,
  input  [7:0] VY,
  input  [11:0] PC,
  input  [11:0] NNN,
  input  [7:0] V0,
  input  [7:0] KK,
  input  [11:0] I,
  input  [7:0] DR,
  input  SCP,
  input  [3:0] K,
  input  _9XY0,
  input  ANNN,
  input  BNNN,
  input  CXKK,
  input  DXYK,
  input  EX9E,
  input  EXA1,
  input  [4:0] CL,
  input  T1,
  input  T2,
  input  H,
  output [11:0] I_2,
  output SI,
  output [7:0] VX_2,
  output SVX,
  output [7:0] DF,
  output SVF,
  output [5:0] SCX,
  output [4:0] SCY,
  output [11:0] AR,
  output SCstore,
  output SSCP,
  output [3:0] AY,
  output [11:0] PC_2,
  output SPC,
  output [3:0] AX,
  output EC,
  output [3:0] NC
);

  wire annn_1_ec, bnnn_1_ec, bnnn_1_spc, cxkk_1_ec, dxyk_1_ec, ex9e_1_ec, ex9e_1_spc, exa1_1_ec, exa1_1_spc,
       n9xy0_1_ec, n9xy0_1_spc;
  wire [3:0] annn_1_nc, bnnn_1_nc, cxkk_1_ax, cxkk_1_nc, dxyk_1_ax, dxyk_1_ay, dxyk_1_nc, ex9e_1_ax,
       ex9e_1_nc, exa1_1_ax, exa1_1_nc, n9xy0_1_ax, n9xy0_1_ay, n9xy0_1_nc;
  wire [11:0] bnnn_1_pc, ex9e_1_pc_2, exa1_1_pc_2, n9xy0_1_pc_2;

  _9XY0 u_9xy0_1 (
    .VX(VX), .VY(VY), .PC(PC), .PC_2(n9xy0_1_pc_2), .SPC(n9xy0_1_spc), .Y(Y), .AY(n9xy0_1_ay), .X(X),
    .AX(n9xy0_1_ax), .EC(n9xy0_1_ec), .T1(T1), .T2(T2), .NC(n9xy0_1_nc), .enable(_9XY0), .H(H));
  ANNN annn_1 (.NNN(NNN), .T1(T1), .enable(ANNN), .I(I_2), .SI(SI), .EC(annn_1_ec), .NC(annn_1_nc), .H(H));
  BNNN bnnn_1 (
    .NNN(NNN), .V0(V0), .T1(T1), .enable(BNNN), .PC(bnnn_1_pc), .SPC(bnnn_1_spc), .EC(bnnn_1_ec),
    .NC(bnnn_1_nc), .H(H));
  CXKK cxkk_1 (
    .X(X), .KK(KK), .T1(T1), .T2(T2), .enable(CXKK), .AX(cxkk_1_ax), .VX(VX_2), .SVX(SVX), .EC(cxkk_1_ec),
    .NC(cxkk_1_nc), .H(H));
  DXYK dxyk_1 (
    .Y(Y), .X(X), .VX(VX), .VY(VY), .I(I), .DR(DR), .SCP(SCP), .B1(K), .H(H), .enable(DXYK), .T1(T1),
    .T2(T2), .AY(dxyk_1_ay), .AX(dxyk_1_ax), .DF(DF), .SVF(SVF), .SCX(SCX), .SCY(SCY), .AR(AR),
    .SCstore(SCstore), .SSCP(SSCP), .EC(dxyk_1_ec), .NC(dxyk_1_nc));
  EX9E ex9e_1 (
    .X(X), .PC(PC), .CL(CL), .VX(VX), .T1(T1), .enable(EX9E), .AX(ex9e_1_ax), .PC_2(ex9e_1_pc_2),
    .SPC(ex9e_1_spc), .EC(ex9e_1_ec), .NC(ex9e_1_nc), .H(H));
  EXA1 exa1_1 (
    .X(X), .PC(PC), .CL(CL), .VX(VX), .T1(T1), .enable(EXA1), .AX(exa1_1_ax), .PC_2(exa1_1_pc_2),
    .SPC(exa1_1_spc), .EC(exa1_1_ec), .NC(exa1_1_nc), .H(H));
  assign AY = n9xy0_1_ay | dxyk_1_ay;  // OR_Gate or_1, 4 bits wide
  assign PC_2 = n9xy0_1_pc_2 | bnnn_1_pc | ex9e_1_pc_2 | exa1_1_pc_2;  // OR_Gate or_2, 12 bits wide
  or or_3 (SPC, n9xy0_1_spc, bnnn_1_spc, ex9e_1_spc, exa1_1_spc);
  assign AX = n9xy0_1_ax | cxkk_1_ax | dxyk_1_ax | ex9e_1_ax | exa1_1_ax;  // OR_Gate or_4, 4 bits wide
  or or_5 (EC, n9xy0_1_ec, annn_1_ec, bnnn_1_ec, cxkk_1_ec, dxyk_1_ec, ex9e_1_ec, exa1_1_ec);
  assign NC = n9xy0_1_nc | annn_1_nc | bnnn_1_nc | cxkk_1_nc | dxyk_1_nc | ex9e_1_nc | exa1_1_nc;  // OR_Gate or_6, 4 bits wide
endmodule

module _9XY0 (
  input  [3:0] Y,
  input  [3:0] X,
  input  [11:0] PC,
  input  [7:0] VX,
  input  [7:0] VY,
  input  T1,
  input  T2,
  input  enable,
  input  H,
  output [3:0] AY,
  output [3:0] AX,
  output [11:0] PC_2,
  output SPC,
  output EC,
  output [3:0] NC
);

  wire and_1_out, and_2_out, and_3_out, and_4_out, comparator_1_eq, not_1_out, not_2_out, or_1_out, savd_1_p5;
  wire [3:0] bit_extender_3_out, bit_extender_4_out, bit_extender_5_out;
  wire [8:0] bit_extender_1_out, bit_extender_2_out;
  wire [11:0] adder_1_out, bit_extender_6_out;

  assign bit_extender_1_out = {{1{1'b0}}, VX};  // Bit_Extender bit_extender_1
  assign bit_extender_2_out = {{1{1'b0}}, VY};  // Bit_Extender bit_extender_2
  Adder #(.width(12)) adder_1 (.a(PC), .b(12'h2), .out(adder_1_out), .cin(1'b0));  // open: cout
  Comparator #(.width(9)) comparator_1 (
    .a(bit_extender_1_out), .b(bit_extender_2_out), .eq(comparator_1_eq));  // open: gt, lt
  not not_1 (not_1_out, comparator_1_eq);
  and and_1 (and_1_out, not_1_out, or_1_out);
  or or_1 (or_1_out, and_2_out, and_3_out);
  and and_2 (and_2_out, enable, T1);
  and and_3 (and_3_out, T2, enable);
  not not_2 (not_2_out, enable);
  and and_4 (and_4_out, and_1_out, and_3_out);
  assign bit_extender_3_out = {{3{enable}}, enable};  // Bit_Extender bit_extender_3
  assign AY = Y & bit_extender_4_out;  // AND_Gate and_5, 4 bits wide
  assign bit_extender_4_out = {{3{enable}}, enable};  // Bit_Extender bit_extender_4
  assign AX = X & bit_extender_5_out;  // AND_Gate and_6, 4 bits wide
  assign bit_extender_5_out = {{3{enable}}, enable};  // Bit_Extender bit_extender_5
  assign PC_2 = adder_1_out & bit_extender_6_out;  // AND_Gate and_7, 12 bits wide
  assign bit_extender_6_out = {{11{and_4_out}}, and_4_out};  // Bit_Extender bit_extender_6
  and and_8 (EC, 1'b1, enable);
  assign NC = 4'b0100 & bit_extender_3_out;  // AND_Gate and_9, 4 bits wide
  // SAVD savd_1: pin names not known; wires that end beside it: H, and_4_out, not_2_out, SPC, savd_1_p5

  // Notes on the sheet:
  //   9xy0 - [  if(Vx!=Vy)         ] - SNE Vx, Vy
  //   Skips the next instruction if VX doesn't equal VY. (Usually the next instruction is a jump to skip a code block)
endmodule

module ANNN (
  input  [11:0] NNN,
  input  T1,
  input  enable,
  input  H,
  output [11:0] I,
  output SI,
  output EC,
  output [3:0] NC
);

  wire and_2_out, not_1_out, savd_1_p5;
  wire [3:0] bit_extender_2_out;
  wire [11:0] bit_extender_1_out;

  assign bit_extender_1_out = {{11{and_2_out}}, and_2_out};  // Bit_Extender bit_extender_1
  assign I = NNN & bit_extender_1_out;  // AND_Gate and_1, 12 bits wide
  and and_2 (and_2_out, T1, enable);
  not not_1 (not_1_out, enable);
  assign bit_extender_2_out = {{3{enable}}, enable};  // Bit_Extender bit_extender_2
  and and_3 (EC, 1'b1, enable);
  assign NC = 4'b0011 & bit_extender_2_out;  // AND_Gate and_4, 4 bits wide
  // SAVD savd_1: pin names not known; wires that end beside it: H, and_2_out, not_1_out, SI, savd_1_p5

  // Notes on the sheet:
  //   Annn - [  I = NNN            ] - LD I, addr
  //   Sets I to the address NNN.
endmodule

module BNNN (
  input  [11:0] NNN,
  input  [7:0] V0,
  input  T1,
  input  enable,
  input  H,
  output [11:0] PC,
  output SPC,
  output EC,
  output [3:0] NC
);

  wire and_1_out, not_1_out, savd_1_p5;
  wire [3:0] bit_extender_5_out;
  wire [11:0] bit_extender_3_out, bit_extender_4_out;
  wire [13:0] adder_1_out, bit_extender_1_out, bit_extender_2_out;

  assign bit_extender_1_out = {{2{1'b0}}, NNN};  // Bit_Extender bit_extender_1
  Adder #(.width(14)) adder_1 (
    .a(bit_extender_1_out), .b(bit_extender_2_out), .out(adder_1_out), .cin(1'b0));  // open: cout
  assign bit_extender_2_out = {{6{1'b0}}, V0};  // Bit_Extender bit_extender_2
  and and_1 (and_1_out, T1, enable);
  Bit_Extender #(.in_width(14), .out_width(12)) bit_extender_3 (.in(adder_1_out), .out(bit_extender_3_out));
  not not_1 (not_1_out, enable);
  assign PC = bit_extender_3_out & bit_extender_4_out;  // AND_Gate and_2, 12 bits wide
  assign bit_extender_4_out = {{11{and_1_out}}, and_1_out};  // Bit_Extender bit_extender_4
  assign bit_extender_5_out = {{3{enable}}, enable};  // Bit_Extender bit_extender_5
  and and_3 (EC, 1'b1, enable);
  assign NC = 4'b0011 & bit_extender_5_out;  // AND_Gate and_4, 4 bits wide
  // SAVD savd_1: pin names not known; wires that end beside it: H, and_1_out, not_1_out, SPC, savd_1_p5

  // Notes on the sheet:
  //   Bnnn - [  PC=V0+NNN          ] - JP V0, addr
  //   Jumps to the address NNN plus V0.
endmodule

module CXKK (
  input  [3:0] X,
  input  [7:0] KK,
  input  T1,
  input  T2,
  input  enable,
  input  H,
  output [3:0] AX,
  output [7:0] VX,
  output SVX,
  output EC,
  output [3:0] NC
);

  wire and_1_out, and_2_out, not_1_out, savd_1_p5;
  wire [3:0] bit_extender_2_out, bit_extender_3_out;
  wire [7:0] bit_extender_1_out, randm_1_output;

  and and_1 (and_1_out, enable, T1);
  and and_2 (and_2_out, T2, enable);
  RANDM randm_1 (.H(and_1_out), .Enable(and_1_out), .Max(KK), .Output(randm_1_output));  // open: def
  not not_1 (not_1_out, enable);
  // Probe on randm_1_output
  assign bit_extender_1_out = {{7{and_2_out}}, and_2_out};  // Bit_Extender bit_extender_1
  assign bit_extender_2_out = {{3{enable}}, enable};  // Bit_Extender bit_extender_2
  assign VX = randm_1_output & bit_extender_1_out;  // AND_Gate and_3, 8 bits wide
  and and_4 (EC, 1'b1, enable);
  assign NC = 4'b0100 & bit_extender_2_out;  // AND_Gate and_5, 4 bits wide
  assign bit_extender_3_out = {{3{enable}}, enable};  // Bit_Extender bit_extender_3
  // SAVD savd_1: pin names not known; wires that end beside it: H, and_2_out, not_1_out, SVX, savd_1_p5
  assign AX = X & bit_extender_3_out;  // AND_Gate and_6, 4 bits wide

  // Notes on the sheet:
  //   Cxkk - [  Vx=rand()&NN       ] - RND Vx, byte
  //   Sets VX to the result of a bitwise and operation on a random number (Typically: 0 to 255) and NN.
endmodule

module DXYK (
  input  [3:0] Y,
  input  [3:0] X,
  input  [7:0] VX,
  input  [7:0] VY,
  input  [11:0] I,
  input  [7:0] DR,
  input  SCP,
  input  [3:0] B1,
  input  H,
  input  enable,
  input  T1,
  input  T2,
  output [3:0] AY,
  output [3:0] AX,
  output [7:0] DF,
  output [4:0] SCY,
  output SVF,
  output [5:0] SCX,
  output [11:0] AR,
  output SCstore,
  output SSCP,
  output EC,
  output [3:0] NC
);

  wire alu_g_1_nc, alu_g_1_scstore, alu_g_1_sscp, alu_g_1_svf, and_1_out, and_2_out, and_11_out, not_1_out,
       not_2_out, or_1_out, savd_1_p4;
  wire [3:0] bit_extender_1_out, bit_extender_2_out, bit_extender_7_out;
  wire [4:0] alu_g_1_scy, bit_extender_3_out;
  wire [5:0] alu_g_1_scx, bit_extender_5_out;
  wire [7:0] alu_g_1_df, bit_extender_4_out;
  wire [11:0] alu_g_1_ar, bit_extender_6_out;

  ALU_G alu_g_1 (
    .VX(VX), .VY(VY), .B1(B1), .I(I), .DR(DR), .SCP(SCP), .enable(and_2_out), .H(H), .SCX(alu_g_1_scx),
    .SCY(alu_g_1_scy), .NC(alu_g_1_nc), .AR(alu_g_1_ar), .SCstore(alu_g_1_scstore), .SSCP(alu_g_1_sscp),
    .SVF(alu_g_1_svf), .DF(alu_g_1_df));  // open: C
  and and_1 (and_1_out, enable, T1);
  and and_2 (and_2_out, T2, enable);
  or or_1 (or_1_out, not_1_out, alu_g_1_nc);
  assign bit_extender_1_out = {{3{enable}}, enable};  // Bit_Extender bit_extender_1
  assign bit_extender_2_out = {{3{enable}}, enable};  // Bit_Extender bit_extender_2
  Bit_Extender #(.in_width(6), .out_width(5)) bit_extender_3 (.in(bit_extender_5_out), .out(bit_extender_3_out));
  not not_1 (not_1_out, and_2_out);
  assign AY = Y & bit_extender_1_out;  // AND_Gate and_3, 4 bits wide
  assign AX = X & bit_extender_2_out;  // AND_Gate and_4, 4 bits wide
  assign bit_extender_4_out = {{7{and_2_out}}, and_2_out};  // Bit_Extender bit_extender_4
  assign SCY = alu_g_1_scy & bit_extender_3_out;  // AND_Gate and_5, 5 bits wide
  assign SCX = alu_g_1_scx & bit_extender_5_out;  // AND_Gate and_6, 6 bits wide
  assign AR = alu_g_1_ar & bit_extender_6_out;  // AND_Gate and_7, 12 bits wide
  and and_8 (SCstore, alu_g_1_scstore, and_2_out);
  and and_9 (SSCP, alu_g_1_sscp, and_2_out);
  not not_2 (not_2_out, enable);
  assign bit_extender_5_out = {{5{and_2_out}}, and_2_out};  // Bit_Extender bit_extender_5
  assign DF = alu_g_1_df & bit_extender_4_out;  // AND_Gate and_10, 8 bits wide
  and and_11 (and_11_out, alu_g_1_svf, and_2_out);
  assign bit_extender_6_out = {{6{bit_extender_5_out[5]}}, bit_extender_5_out};  // Bit_Extender bit_extender_6
  assign bit_extender_7_out = {{3{enable}}, enable};  // Bit_Extender bit_extender_7
  // SAVD savd_1: pin names not known; wires that end beside it: H, and_11_out, not_2_out, savd_1_p4
  and and_12 (EC, or_1_out, enable);
  assign NC = 4'b0100 & bit_extender_7_out;  // AND_Gate and_13, 4 bits wide
  or or_2 (SVF, savd_1_p4, and_1_out);

  // Notes on the sheet:
  //   enable: pull=down
  //   B1: pull=down
  //   T2: pull=down
  //   H: pull=down
  //   I: pull=down
  //   VX: pull=down
  //   Y: pull=down
  //   DR: pull=down
  //   X: pull=down
  //   VY: pull=down
  //   SCP: pull=down
  //   T1: pull=down
  //   Dxyn - [  draw(Vx,Vy,N)      ] - DRW Vx, Vy, nibble
  //   Draws a sprite at coordinate (VX, VY) that has a width of 8 pixels and a height of N pixels. Each row of 8 pixels is read as bit-coded starting from memory location I;
  //   I value doesn’t change after the execution of this instruction.
  //   As described above, VF is set to 1 if any screen pixels are flipped from set to unset when the sprite is drawn, and to 0 if that doesn’t happen
endmodule

module EX9E (
  input  [3:0] X,
  input  [11:0] PC,
  input  [4:0] CL,
  input  [7:0] VX,
  input  H,
  input  T1,
  input  enable,
  output [3:0] AX,
  output [11:0] PC_2,
  output SPC,
  output EC,
  output [3:0] NC
);

  wire and_1_out, and_2_out, and_3_out, and_4_out, comparator_1_eq, not_1_out, savd_1_p5;
  wire [3:0] bit_extender_3_out, bit_extender_5_out;
  wire [4:0] bit_extender_1_out, bit_extender_2_out;
  wire [11:0] adder_1_out, bit_extender_4_out;

  assign bit_extender_1_out = {{1{1'b0}}, CL[3:0]};  // Bit_Extender bit_extender_1
  Comparator #(.width(5)) comparator_1 (
    .a(bit_extender_1_out), .b(bit_extender_2_out), .eq(comparator_1_eq));  // open: gt, lt
  Bit_Extender #(.out_width(5)) bit_extender_2 (.in(VX), .out(bit_extender_2_out));
  Adder #(.width(12)) adder_1 (.a(PC), .b(12'h2), .out(adder_1_out), .cin(1'b0));  // open: cout
  and and_1 (and_1_out, CL[4], comparator_1_eq);
  and and_2 (and_2_out, T1, enable);
  and and_3 (and_3_out, and_1_out, enable);
  and and_4 (and_4_out, and_3_out, and_2_out);
  not not_1 (not_1_out, enable);
  assign bit_extender_3_out = {{3{enable}}, enable};  // Bit_Extender bit_extender_3
  assign bit_extender_4_out = {{11{and_4_out}}, and_4_out};  // Bit_Extender bit_extender_4
  assign bit_extender_5_out = {{3{enable}}, enable};  // Bit_Extender bit_extender_5
  assign AX = X & bit_extender_3_out;  // AND_Gate and_5, 4 bits wide
  assign PC_2 = adder_1_out & bit_extender_4_out;  // AND_Gate and_6, 12 bits wide
  and and_7 (EC, 1'b1, enable);
  assign NC = 4'b0011 & bit_extender_5_out;  // AND_Gate and_8, 4 bits wide
  // SAVD savd_1: pin names not known; wires that end beside it: H, and_4_out, not_1_out, SPC, savd_1_p5

  // Notes on the sheet:
  //   Ex9E - [  if(key()==Vx)      ] - SKP Vx
  //   Skips the next instruction if the key stored in VX is pressed. (Usually the next instruction is a jump to skip a code block)
endmodule

module EXA1 (
  input  [3:0] X,
  input  [11:0] PC,
  input  [4:0] CL,
  input  [7:0] VX,
  input  T1,
  input  enable,
  input  H,
  output [3:0] AX,
  output [11:0] PC_2,
  output SPC,
  output EC,
  output [3:0] NC
);

  wire and_1_out, and_2_out, and_3_out, and_5_out, comparator_1_gt, comparator_1_lt, not_1_out, not_2_out,
       or_1_out, or_2_out, savd_1_p5;
  wire [3:0] bit_extender_4_out, bit_extender_5_out;
  wire [4:0] bit_extender_1_out, bit_extender_2_out;
  wire [11:0] adder_1_out, bit_extender_3_out;

  assign bit_extender_1_out = {{1{1'b0}}, CL[3:0]};  // Bit_Extender bit_extender_1
  Comparator #(.width(5)) comparator_1 (
    .a(bit_extender_1_out), .b(bit_extender_2_out), .gt(comparator_1_gt), .lt(comparator_1_lt));  // open: eq
  Bit_Extender #(.out_width(5)) bit_extender_2 (.in(VX), .out(bit_extender_2_out));
  Adder #(.width(12)) adder_1 (.a(PC), .b(12'h2), .out(adder_1_out), .cin(1'b0));  // open: cout
  not not_1 (not_1_out, CL[4]);
  or or_1 (or_1_out, comparator_1_gt, comparator_1_lt);
  and and_1 (and_1_out, T1, enable);
  or or_2 (or_2_out, not_1_out, and_2_out);
  and and_2 (and_2_out, CL[4], or_1_out);
  and and_3 (and_3_out, or_2_out, enable);
  assign bit_extender_3_out = {{11{and_5_out}}, and_5_out};  // Bit_Extender bit_extender_3
  not not_2 (not_2_out, enable);
  assign bit_extender_4_out = {{3{enable}}, enable};  // Bit_Extender bit_extender_4
  assign PC_2 = adder_1_out & bit_extender_3_out;  // AND_Gate and_4, 12 bits wide
  and and_5 (and_5_out, and_3_out, and_1_out);
  assign bit_extender_5_out = {{3{enable}}, enable};  // Bit_Extender bit_extender_5
  assign AX = X & bit_extender_4_out;  // AND_Gate and_6, 4 bits wide
  and and_7 (EC, 1'b1, enable);
  assign NC = 4'b0011 & bit_extender_5_out;  // AND_Gate and_8, 4 bits wide
  // SAVD savd_1: pin names not known; wires that end beside it: H, and_5_out, not_2_out, SPC, savd_1_p5

  // Notes on the sheet:
  //   ExA1 - [  if(key()!=Vx)      ] - SKNP Vx
  //   Skips the next instruction if the key stored in VX isn't pressed. (Usually the next instruction is a jump to skip a code block)
endmodule
