// Logisim project mini_chip8_alu411.circ as structural Verilog: 10 circuits, main circuit FX0A
module ALU4 (
  input  [3:0] X,
  input  [7:0] CMPGAME,
  input  [4:0] CL,
  input  [7:0] VX,
  input  [11:0] I,
  input  [7:0] DR,
  input  FX07,
  input  FX0A,
  input  FX15,
  input  FX18,
  input  FX1E,
  input  FX29,
  input  FX33,
  input  FX55,
  input  FX65,
  input  [7:0] CMPSON,
  input  H,
  input  T1,
  input  T2,
  output [7:0] CMPGAME_2,
  output SCMPGAME,
  output SON,
  output [7:0] CMPSON_2,
  output SCMPSON,
  output [7:0] VF,
  output SVF,
  output [11:0] I_2,
  output SI,
  output [7:0] DR_2,
  output SR,
  output [11:0] AR,
  output [7:0] VX_2,
  output SVX,
  output [3:0] AX,
  output EC,
  output [3:0] NC
);

  wire fx0a_1_ec, fx0a_1_svx, fx1e_1_ec, fx1e_1_si, fx07_1_ec, fx07_1_svx, fx15_1_ec, fx18_1_ec, fx29_1_ec,
       fx29_1_si, fx33_1_ec, fx33_1_sr, fx55_1_ec, fx55_1_sr, fx65_1_ec, fx65_1_sx;
  wire [3:0] fx0a_1_ax, fx0a_1_nc, fx1e_1_ax, fx1e_1_nc, fx07_1_ax, fx07_1_nc, fx15_1_ax, fx15_1_nc,
       fx18_1_ax, fx18_1_nc, fx29_1_ax, fx29_1_nc, fx33_1_ax, fx33_1_nc, fx55_1_ax, fx55_1_nc, fx65_1_ax,
       fx65_1_nc;
  wire [7:0] fx0a_1_vx, fx07_1_vx, fx33_1_dr, fx55_1_dr, fx65_1_dx;
  wire [11:0] fx1e_1_i_2, fx29_1_i, fx33_1_ar, fx55_1_ar, fx65_1_ar;

  FX07 fx07_1 (
    .X(X), .CMPGAME(CMPGAME), .T1(T1), .enable(FX07), .AX(fx07_1_ax), .VX(fx07_1_vx), .SVX(fx07_1_svx),
    .EC(fx07_1_ec), .NC(fx07_1_nc), .H(H));
  FX0A fx0a_1 (
    .X(X), .CL(CL), .T1(T1), .enable(FX0A), .AX(fx0a_1_ax), .VX(fx0a_1_vx), .SVX(fx0a_1_svx), .EC(fx0a_1_ec),
    .NC(fx0a_1_nc), .H(H));
  FX15 fx15_1 (
    .X(X), .VX(VX), .T1(T1), .enable(FX15), .AX(fx15_1_ax), .CMPGAME_2(CMPGAME_2), .SCMPGAME(SCMPGAME),
    .EC(fx15_1_ec), .NC(fx15_1_nc), .H(H), .T2(T2), .CMPGAME(CMPGAME));
  FX18 fx18_1 (
    .X(X), .VX(VX), .T1(T1), .enable(FX18), .AX(fx18_1_ax), .CMPSON_2(CMPSON_2), .SCMPSON(SCMPSON),
    .EC(fx18_1_ec), .NC(fx18_1_nc), .H(H), .CMPSON(CMPSON), .T2(T2), .son(SON));
  FX1E fx1e_1 (
    .X(X), .I(I), .VX(VX), .T1(T1), .enable(FX1E), .AX(fx1e_1_ax), .VF(VF), .SVF(SVF), .I_2(fx1e_1_i_2),
    .SI(fx1e_1_si), .EC(fx1e_1_ec), .NC(fx1e_1_nc), .H(H));
  FX29 fx29_1 (
    .X(X), .VX(VX), .T1(T1), .enable(FX29), .AX(fx29_1_ax), .I(fx29_1_i), .SI(fx29_1_si), .EC(fx29_1_ec),
    .NC(fx29_1_nc), .H(H));
  FX33 fx33_1 (
    .X(X), .VX(VX), .I(I), .H(H), .T1(T1), .enable(FX33), .AX(fx33_1_ax), .DR(fx33_1_dr), .SR(fx33_1_sr),
    .AR(fx33_1_ar), .EC(fx33_1_ec), .NC(fx33_1_nc));
  FX55 fx55_1 (
    .DX(VX), .I(I), .X(X), .H(H), .enable(FX55), .T1(T1), .DR(fx55_1_dr), .AR(fx55_1_ar), .SR(fx55_1_sr),
    .AX(fx55_1_ax), .EC(fx55_1_ec), .NC(fx55_1_nc));
  FX65 fx65_1 (
    .DR(DR), .I(I), .X(X), .H(H), .enable(FX65), .T1(T1), .DX(fx65_1_dx), .AR(fx65_1_ar), .SX(fx65_1_sx),
    .AX(fx65_1_ax), .EC(fx65_1_ec), .NC(fx65_1_nc));
  assign I_2 = fx1e_1_i_2 | fx29_1_i;  // OR_Gate or_1, 12 bits wide
  or or_2 (SI, fx1e_1_si, fx29_1_si);
  assign DR_2 = fx33_1_dr | fx55_1_dr;  // OR_Gate or_3, 8 bits wide
  or or_4 (SR, fx33_1_sr, fx55_1_sr);
  assign AR = fx33_1_ar | fx55_1_ar | fx65_1_ar;  // OR_Gate or_5, 12 bits wide
  assign VX_2 = fx07_1_vx | fx0a_1_vx | fx65_1_dx;  // OR_Gate or_6, 8 bits wide
  or or_7 (SVX, fx07_1_svx, fx0a_1_svx, fx65_1_sx);
  assign AX = fx07_1_ax | fx0a_1_ax | fx15_1_ax | fx18_1_ax | fx1e_1_ax | fx29_1_ax | fx33_1_ax | fx55_1_ax | fx65_1_ax;  // OR_Gate or_8, 4 bits wide
  or or_9 (EC, fx07_1_ec, fx0a_1_ec, fx15_1_ec, fx18_1_ec, fx1e_1_ec, fx29_1_ec, fx33_1_ec, fx55_1_ec, fx65_1_ec);
  assign NC = fx07_1_nc | fx0a_1_nc | fx15_1_nc | fx18_1_nc | fx1e_1_nc | fx29_1_nc | fx33_1_nc | fx55_1_nc | fx65_1_nc;  // OR_Gate or_10, 4 bits wide
endmodule

module FX07 (
  input  [3:0] X,
  input  [7:0] CMPGAME,
  input  H,
  input  T1,
  input  enable,
  output [3:0] AX,
  output [7:0] VX,
  output SVX,
  output [3:0] NC,
  output EC
);

  wire and_2_out, not_1_out, savd_1_p5;
  wire [3:0] bit_extender_2_out, bit_extender_3_out;
  wire [7:0] bit_extender_1_out;

  assign bit_extender_1_out = {{7{and_2_out}}, and_2_out};  // Bit_Extender bit_extender_1
  assign VX = CMPGAME & bit_extender_1_out;  // AND_Gate and_1, 8 bits wide
  and and_2 (and_2_out, T1, enable);
  not not_1 (not_1_out, enable);
  assign bit_extender_2_out = {{3{enable}}, enable};  // Bit_Extender bit_extender_2
  assign bit_extender_3_out = {{3{enable}}, enable};  // Bit_Extender bit_extender_3
  assign NC = 4'b0011 & bit_extender_2_out;  // AND_Gate and_3, 4 bits wide
  and and_4 (EC, 1'b1, enable);
  assign AX = X & bit_extender_3_out;  // AND_Gate and_5, 4 bits wide
  // SAVD savd_1: pin names not known; wires that end beside it: H, and_2_out, not_1_out, SVX, savd_1_p5

  // Notes on the sheet:
  //   Fx07 - [  Vx = get_delay()   ] - LD Vx, DT
  //   Sets VX to the value of the delay timer.
endmodule

module FX0A (
  input  [3:0] X,
  input  [4:0] CL,
  input  H,
  input  T1,
  input  enable,
  output [3:0] AX,
  output [7:0] VX,
  output SVX,
  output EC,
  output [3:0] NC
);

  wire and_1_out, not_1_out, savd_1_p5;
  wire [3:0] and_2_out, bit_extender_3_out, bit_extender_4_out;
  wire [7:0] bit_extender_1_out, bit_extender_2_out;

  and and_1 (and_1_out, T1, enable);
  assign and_2_out = CL[3:0] & bit_extender_3_out;  // AND_Gate and_2, 4 bits wide
  assign bit_extender_1_out = {{4{1'b0}}, and_2_out};  // Bit_Extender bit_extender_1
  assign VX = bit_extender_1_out & bit_extender_2_out;  // AND_Gate and_3, 8 bits wide
  assign bit_extender_2_out = {{7{and_1_out}}, and_1_out};  // Bit_Extender bit_extender_2
  assign bit_extender_3_out = {{3{enable}}, enable};  // Bit_Extender bit_extender_3
  not not_1 (not_1_out, enable);
  assign AX = X & bit_extender_4_out;  // AND_Gate and_4, 4 bits wide
  assign bit_extender_4_out = {{3{enable}}, enable};  // Bit_Extender bit_extender_4
  and and_5 (EC, CL[4], enable);
  assign NC = 4'b0011 & bit_extender_3_out;  // AND_Gate and_6, 4 bits wide
  // SAVD savd_1: pin names not known; wires that end beside it: H, and_1_out, not_1_out, SVX, savd_1_p5

  // Notes on the sheet:
  //   Fx0A - [  Vx = get_key()     ] - LD Vx, K
  //   A key press is awaited, and then stored in VX. (Blocking Operation. All instruction halted until next key event)
endmodule

module FX15 (
  input  [3:0] X,
  input  [7:0] VX,
  input  [7:0] CMPGAME,
  input  H,
  input  T2,
  input  T1,
  input  enable,
  output [3:0] AX,
  output [7:0] CMPGAME_2,
  output SCMPGAME,
  output EC,
  output [3:0] NC
);

  wire and_2_out, and_3_out, and_4_out, and_5_out, and_6_out, and_8_out, comparator_1_eq, comparator_1_gt,
       not_1_out, not_2_out, not_3_out, or_1_out, or_2_out, savd_1_p5;
  wire [3:0] bit_extender_5_out, bit_extender_6_out;
  wire [7:0] and_1_out, and_7_out, bit_extender_2_out, bit_extender_3_out, bit_extender_4_out;
  wire [8:0] bit_extender_1_out, subtractor_1_out;

  assign bit_extender_1_out = {{1{1'b0}}, CMPGAME};  // Bit_Extender bit_extender_1
  assign and_1_out = VX & bit_extender_2_out;  // AND_Gate and_1, 8 bits wide
  assign bit_extender_2_out = {{7{and_3_out}}, and_3_out};  // Bit_Extender bit_extender_2
  Comparator #(.width(9)) comparator_1 (
    .a(bit_extender_1_out), .b({9{1'b0}}), .gt(comparator_1_gt), .eq(comparator_1_eq));  // open: lt
  Subtractor #(.width(9)) subtractor_1 (
    .a(bit_extender_1_out), .b(9'h1), .out(subtractor_1_out), .bin(1'b0));  // open: bout
  and and_2 (and_2_out, T2, enable);
  and and_3 (and_3_out, T1, enable);
  Bit_Extender #(.in_width(9), .out_width(8)) bit_extender_3 (.in(subtractor_1_out), .out(bit_extender_3_out));
  and and_4 (and_4_out, comparator_1_gt, and_2_out);
  not not_1 (not_1_out, and_2_out);
  assign bit_extender_4_out = {{7{and_8_out}}, and_8_out};  // Bit_Extender bit_extender_4
  or or_1 (or_1_out, and_3_out, and_4_out);
  not not_2 (not_2_out, comparator_1_eq);
  and and_5 (and_5_out, comparator_1_eq, and_2_out);
  or or_2 (or_2_out, and_5_out, and_6_out);
  and and_6 (and_6_out, not_1_out, 1'b1);
  assign bit_extender_5_out = {{3{enable}}, enable};  // Bit_Extender bit_extender_5
  assign bit_extender_6_out = {{3{enable}}, enable};  // Bit_Extender bit_extender_6
  assign CMPGAME_2 = and_1_out | and_7_out;  // OR_Gate or_3, 8 bits wide
  assign and_7_out = bit_extender_3_out & bit_extender_4_out;  // AND_Gate and_7, 8 bits wide
  and and_8 (and_8_out, or_1_out, not_2_out);
  not not_3 (not_3_out, enable);
  and and_9 (EC, or_2_out, enable);
  assign NC = 4'b0100 & bit_extender_5_out;  // AND_Gate and_10, 4 bits wide
  assign AX = X & bit_extender_6_out;  // AND_Gate and_11, 4 bits wide
  // SAVD savd_1: pin names not known; wires that end beside it: H, or_1_out, not_3_out, SCMPGAME, savd_1_p5

  // Notes on the sheet:
  //   Fx15 - [  delay_timer(Vx)    ] - LD DT, Vx
  //   Sets the delay timer to VX.
endmodule

module FX18 (
  input  [3:0] X,
  input  [7:0] VX,
  input  [7:0] CMPSON,
  input  H,
  input  T2,
  input  T1,
  input  enable,
  output [3:0] AX,
  output [7:0] CMPSON_2,
  output SCMPSON,
  output son,
  output EC,
  output [3:0] NC
);

  wire and_2_out, and_3_out, and_4_out, and_5_out, and_6_out, and_8_out, comparator_1_eq, not_1_out,
       not_2_out, not_3_out, or_1_out, or_2_out, savd_1_p5;
  wire [3:0] bit_extender_5_out, bit_extender_6_out;
  wire [7:0] and_1_out, and_7_out, bit_extender_1_out, bit_extender_3_out, bit_extender_4_out;
  wire [8:0] bit_extender_2_out, subtractor_1_out;

  assign bit_extender_1_out = {{7{and_3_out}}, and_3_out};  // Bit_Extender bit_extender_1
  assign bit_extender_2_out = {{1{1'b0}}, CMPSON};  // Bit_Extender bit_extender_2
  assign and_1_out = VX & bit_extender_1_out;  // AND_Gate and_1, 8 bits wide
  Comparator #(.width(9)) comparator_1 (
    .a(bit_extender_2_out), .b({9{1'b0}}), .gt(son), .eq(comparator_1_eq));  // open: lt
  Subtractor #(.width(9)) subtractor_1 (
    .a(bit_extender_2_out), .b(9'h1), .out(subtractor_1_out), .bin(1'b0));  // open: bout
  and and_2 (and_2_out, T2, enable);
  and and_3 (and_3_out, T1, enable);
  and and_4 (and_4_out, son, and_2_out);
  Bit_Extender #(.in_width(9), .out_width(8)) bit_extender_3 (.in(subtractor_1_out), .out(bit_extender_3_out));
  not not_1 (not_1_out, and_2_out);
  and and_5 (and_5_out, comparator_1_eq, and_2_out);
  and and_6 (and_6_out, not_1_out, 1'b1);
  assign and_7_out = bit_extender_3_out & bit_extender_4_out;  // AND_Gate and_7, 8 bits wide
  assign bit_extender_4_out = {{7{and_8_out}}, and_8_out};  // Bit_Extender bit_extender_4
  or or_1 (or_1_out, and_3_out, and_4_out);
  not not_2 (not_2_out, comparator_1_eq);
  not not_3 (not_3_out, enable);
  or or_2 (or_2_out, and_5_out, and_6_out);
  assign bit_extender_5_out = {{3{enable}}, enable};  // Bit_Extender bit_extender_5
  assign bit_extender_6_out = {{3{enable}}, enable};  // Bit_Extender bit_extender_6
  assign CMPSON_2 = and_1_out | and_7_out;  // OR_Gate or_3, 8 bits wide
  and and_8 (and_8_out, or_1_out, not_2_out);
  and and_9 (EC, or_2_out, enable);
  assign NC = 4'b0100 & bit_extender_5_out;  // AND_Gate and_10, 4 bits wide
  assign AX = X & bit_extender_6_out;  // AND_Gate and_11, 4 bits wide
  // SAVD savd_1: pin names not known; wires that end beside it: H, or_1_out, not_3_out, SCMPSON, savd_1_p5

  // Notes on the sheet:
  //   Fx18 - [  sound_timer(Vx)    ] - LD ST, Vx
  //   Sets the sound timer to VX.
endmodule

module FX1E (
  input  [3:0] X,
  input  [11:0] I,
  input  [7:0] VX,
  input  H,
  input  T1,
  input  enable,
  output [3:0] AX,
  output [7:0] VF,
  output SVF,
  output [11:0] I_2,
  output SI,
  output EC,
  output [3:0] NC
);

  wire adder_1_cout, and_1_out, not_1_out, savd_2_p5;
  wire [3:0] bit_extender_2_out, bit_extender_6_out;
  wire [7:0] bit_extender_3_out, bit_extender_4_out;
  wire [11:0] adder_1_out, bit_extender_1_out, bit_extender_5_out;

  assign bit_extender_1_out = {{4{1'b0}}, VX};  // Bit_Extender bit_extender_1
  Adder #(.width(12)) adder_1 (.a(I), .b(bit_extender_1_out), .out(adder_1_out), .cin(1'b0), .cout(adder_1_cout));
  and and_1 (and_1_out, T1, enable);
  assign bit_extender_2_out = {{3{enable}}, enable};  // Bit_Extender bit_extender_2
  assign bit_extender_3_out = {{7{1'b0}}, adder_1_cout};  // Bit_Extender bit_extender_3
  assign bit_extender_4_out = {{7{and_1_out}}, and_1_out};  // Bit_Extender bit_extender_4
  assign bit_extender_5_out = {{11{and_1_out}}, and_1_out};  // Bit_Extender bit_extender_5
  assign I_2 = adder_1_out & bit_extender_5_out;  // AND_Gate and_2, 12 bits wide
  not not_1 (not_1_out, enable);
  and and_3 (EC, 1'b1, enable);
  assign NC = 4'b0011 & bit_extender_6_out;  // AND_Gate and_4, 4 bits wide
  assign bit_extender_6_out = {{3{enable}}, enable};  // Bit_Extender bit_extender_6
  assign AX = X & bit_extender_2_out;  // AND_Gate and_5, 4 bits wide
  assign VF = bit_extender_3_out & bit_extender_4_out;  // AND_Gate and_6, 8 bits wide
  // SAVD savd_1: pin names not known; wires that end beside it: H, and_1_out, not_1_out, SVF
  // SAVD savd_2: pin names not known; wires that end beside it: H, and_1_out, not_1_out, SI, savd_2_p5

  // Notes on the sheet:
  //   Fx1E - [  I +=Vx             ] - ADD I, Vx
  //   Adds VX to I. VF is set to 1 when there is a range overflow (I+VX>0xFFF), and to 0 when there isn't.
endmodule

module FX29 (
  input  [3:0] X,
  input  [7:0] VX,
  input  H,
  input  T1,
  input  enable,
  output [3:0] AX,
  output [11:0] I,
  output SI,
  output EC,
  output [3:0] NC
);

  wire and_1_out, not_1_out, savd_1_p5;
  wire [3:0] bit_extender_2_out, bit_extender_4_out;
  wire [11:0] adder_1_out, bit_extender_1_out, bit_extender_3_out, multiplier_1_out;

  assign bit_extender_1_out = {{4{1'b0}}, VX};  // Bit_Extender bit_extender_1
  and and_1 (and_1_out, T1, enable);
  Multiplier #(.width(12)) multiplier_1 (
    .a(bit_extender_1_out), .b(12'h5), .out(multiplier_1_out), .cin({12{1'b0}}));  // open: cout
  Adder #(.width(12)) adder_1 (.a(multiplier_1_out), .b(12'h4), .out(adder_1_out), .cin(1'b0));  // open: cout
  assign bit_extender_2_out = {{3{enable}}, enable};  // Bit_Extender bit_extender_2
  assign bit_extender_3_out = {{11{and_1_out}}, and_1_out};  // Bit_Extender bit_extender_3
  not not_1 (not_1_out, enable);
  assign bit_extender_4_out = {{3{enable}}, enable};  // Bit_Extender bit_extender_4
  assign AX = X & bit_extender_2_out;  // AND_Gate and_2, 4 bits wide
  assign I = adder_1_out & bit_extender_3_out;  // AND_Gate and_3, 12 bits wide
  and and_4 (EC, 1'b1, enable);
  assign NC = 4'b0011 & bit_extender_4_out;  // AND_Gate and_5, 4 bits wide
  // SAVD savd_1: pin names not known; wires that end beside it: H, and_1_out, not_1_out, SI, savd_1_p5

  // Notes on the sheet:
  //   Fx29 - [  I=sprite_addr[Vx]  ] - LD F, Vx
  //   Sets I to the location of the sprite for the character in VX. Characters 0-F (in hexadecimal) are represented by a 4x5 font.
endmodule

module FX33 (
  input  [3:0] X,
  input  [7:0] VX,
  input  [11:0] I,
  input  H,
  input  T1,
  input  enable,
  output [3:0] AX,
  output [7:0] DR,
  output SR,
  output [11:0] AR,
  output EC,
  output [3:0] NC
);

  wire aluhexdec_1_p1, aluhexdec_1_p7, aluhexdec_1_p9, and_2_out, and_3_out, not_1_out, not_2_out, or_1_out;
  wire [3:0] bit_extender_1_out, bit_extender_2_out;

  assign AX = X & bit_extender_1_out;  // AND_Gate and_1, 4 bits wide
  assign bit_extender_1_out = {{3{enable}}, enable};  // Bit_Extender bit_extender_1
  // aluHexDec aluhexdec_1: pin names not known; wires that end beside it: aluhexdec_1_p1, VX, I, H, enable, DR, aluhexdec_1_p7, AR, aluhexdec_1_p9
  not not_1 (not_1_out, enable);
  not not_2 (not_2_out, and_2_out);
  and and_2 (and_2_out, T1, enable);
  or or_1 (or_1_out, aluhexdec_1_p9, not_2_out);
  assign bit_extender_2_out = {{3{enable}}, enable};  // Bit_Extender bit_extender_2
  and and_3 (and_3_out, or_1_out, enable);
  assign NC = 4'b0011 & bit_extender_2_out;  // AND_Gate and_4, 4 bits wide
  // SAVD savd_1: pin names not known; wires that end beside it: H, aluhexdec_1_p7, not_1_out, SR
  // SAVD savd_2: pin names not known; wires that end beside it: H, and_3_out, not_1_out, EC, aluhexdec_1_p1

  // Notes on the sheet:
  //   Fx33 - [  set_BCD(Vx)        ] - LD B, Vx
  //   Stores the binary-coded decimal representation of VX, with the most significant of three digits at the address in I, the middle digit at I plus 1, and the least significant digit at I plus 2.
  //   (In other words, take the decimal representation of VX, place the hundreds digit in memory at location in I, the tens digit at location I+1, and the ones digit at location I+2.).
  //   [*(I+0)=BCD(3); *(I+1)=BCD(2); *(I+2)=BCD(1);]
endmodule

module FX55 (
  input  [7:0] DX,
  input  [11:0] I,
  input  [3:0] X,
  input  H,
  input  T1,
  input  enable,
  output [7:0] DR,
  output [11:0] AR,
  output SR,
  output [3:0] AX,
  output EC,
  output [3:0] NC
);

  wire and_1_out, and_2_out, and_3_out, and_8_out, comparator_1_eq, comparator_1_gt, comparator_1_lt,
       not_1_out, not_2_out, not_3_out, or_1_out, or_2_out, or_3_out;
  wire [3:0] bit_extender_3_out, bit_extender_4_out, bit_extender_7_out;
  wire [5:0] bit_extender_1_out;
  wire [7:0] bit_extender_5_out, counter_1_q;
  wire [11:0] adder_1_out, bit_extender_2_out, bit_extender_6_out;

  and and_1 (and_1_out, enable, or_2_out);
  not not_1 (not_1_out, enable);
  and and_2 (and_2_out, T1, enable);
  Counter counter_1 (
    .load(1'b0), .D({8{1'b0}}), .count(and_1_out), .Q(counter_1_q), .clk(and_3_out), .clr(not_1_out));  // open: carry
  assign bit_extender_1_out = {{2{1'b0}}, X};  // Bit_Extender bit_extender_1
  and and_3 (and_3_out, or_2_out, H);
  assign bit_extender_2_out = {{6{1'b0}}, counter_1_q[7:2]};  // Bit_Extender bit_extender_2
  Comparator #(.width(6)) comparator_1 (
    .a(counter_1_q[7:2]), .b(bit_extender_1_out), .gt(comparator_1_gt), .eq(comparator_1_eq),
    .lt(comparator_1_lt));
  Adder #(.width(12)) adder_1 (.a(I), .b(bit_extender_2_out), .out(adder_1_out), .cin(1'b0));  // open: cout
  Bit_Extender #(.in_width(6), .out_width(4)) bit_extender_3 (.in(counter_1_q[7:2]), .out(bit_extender_3_out));
  or or_1 (or_1_out, counter_1_q[0], counter_1_q[1]);
  or or_2 (or_2_out, comparator_1_lt, comparator_1_eq);
  not not_2 (not_2_out, and_2_out);
  or or_3 (or_3_out, not_2_out, comparator_1_gt);
  and and_4 (EC, or_3_out, enable);
  assign bit_extender_4_out = {{3{enable}}, enable};  // Bit_Extender bit_extender_4
  assign bit_extender_5_out = {{7{and_2_out}}, and_2_out};  // Bit_Extender bit_extender_5
  assign bit_extender_6_out = {{11{and_2_out}}, and_2_out};  // Bit_Extender bit_extender_6
  assign bit_extender_7_out = {{3{and_2_out}}, and_2_out};  // Bit_Extender bit_extender_7
  not not_3 (not_3_out, EC);
  assign NC = 4'b0011 & bit_extender_4_out;  // AND_Gate and_5, 4 bits wide
  assign DR = DX & bit_extender_5_out;  // AND_Gate and_6, 8 bits wide
  assign AR = adder_1_out & bit_extender_6_out;  // AND_Gate and_7, 12 bits wide
  and and_8 (and_8_out, and_2_out, not_3_out, or_1_out);
  assign AX = bit_extender_3_out & bit_extender_7_out;  // AND_Gate and_9, 4 bits wide
  // SAVD savd_1: pin names not known; wires that end beside it: H, and_8_out, not_1_out, SR

  // Notes on the sheet:
  //   Fx55 - [  reg_dump(Vx,&I)    ] - LD [I], Vx
  //   Stores V0 to VX (including VX) in memory starting at address I. The offset from I is increased by 1 for each value written, but I itself is left unmodified.
endmodule

module FX65 (
  input  [7:0] DR,
  input  [11:0] I,
  input  [3:0] X,
  input  H,
  input  T1,
  input  enable,
  output [7:0] DX,
  output [11:0] AR,
  output SX,
  output [3:0] AX,
  output EC,
  output [3:0] NC
);

  wire and_1_out, and_2_out, and_3_out, and_4_out, and_7_out, and_9_out, comparator_1_eq, comparator_1_gt,
       comparator_1_lt, not_1_out, not_2_out, or_1_out, or_2_out, or_3_out, or_4_out;
  wire [3:0] bit_extender_3_out, bit_extender_6_out, bit_extender_7_out;
  wire [5:0] bit_extender_1_out;
  wire [7:0] bit_extender_4_out, counter_1_q;
  wire [11:0] adder_1_out, bit_extender_2_out, bit_extender_5_out;

  assign bit_extender_1_out = {{2{1'b0}}, X};  // Bit_Extender bit_extender_1
  and and_1 (and_1_out, enable, or_1_out);
  not not_1 (not_1_out, enable);
  and and_2 (and_2_out, enable, T1);
  Counter counter_1 (
    .load(1'b0), .D({8{1'b0}}), .count(and_1_out), .Q(counter_1_q), .clk(and_3_out), .clr(not_1_out));  // open: carry
  and and_3 (and_3_out, or_1_out, H);
  assign bit_extender_2_out = {{6{1'b0}}, counter_1_q[7:2]};  // Bit_Extender bit_extender_2
  Bit_Extender #(.in_width(6), .out_width(4)) bit_extender_3 (.in(counter_1_q[7:2]), .out(bit_extender_3_out));
  Comparator #(.width(6)) comparator_1 (
    .a(counter_1_q[7:2]), .b(bit_extender_1_out), .gt(comparator_1_gt), .eq(comparator_1_eq),
    .lt(comparator_1_lt));
  Adder #(.width(12)) adder_1 (.a(I), .b(bit_extender_2_out), .out(adder_1_out), .cin(1'b0));  // open: cout
  or or_1 (or_1_out, comparator_1_lt, comparator_1_eq);
  or or_2 (or_2_out, counter_1_q[0], counter_1_q[1]);
  not not_2 (not_2_out, and_2_out);
  and and_4 (and_4_out, or_2_out, or_1_out);
  or or_3 (or_3_out, not_2_out, comparator_1_gt);
  assign bit_extender_4_out = {{7{and_2_out}}, and_2_out};  // Bit_Extender bit_extender_4
  assign bit_extender_5_out = {{11{and_2_out}}, and_2_out};  // Bit_Extender bit_extender_5
  assign bit_extender_6_out = {{3{and_2_out}}, and_2_out};  // Bit_Extender bit_extender_6
  assign bit_extender_7_out = {{3{enable}}, enable};  // Bit_Extender bit_extender_7
  assign DX = DR & bit_extender_4_out;  // AND_Gate and_5, 8 bits wide
  assign AR = adder_1_out & bit_extender_5_out;  // AND_Gate and_6, 12 bits wide
  and and_7 (and_7_out, and_2_out, and_4_out);
  assign AX = bit_extender_3_out & bit_extender_6_out;  // AND_Gate and_8, 4 bits wide
  and and_9 (and_9_out, or_1_out, H);
  or or_4 (or_4_out, counter_1_q[0], not_1_out);
  and and_10 (EC, or_3_out, enable);
  assign NC = 4'b0011 & bit_extender_7_out;  // AND_Gate and_11, 4 bits wide
  // SAVD savd_1: pin names not known; wires that end beside it: and_9_out, and_7_out, or_4_out, SX

  // Notes on the sheet:
  //   Fx65 - [  reg_load(Vx,&I)    ] - LD Vx, [I]
  //   Fills V0 to VX (including VX) with values from memory starting at address I. The offset from I is increased by 1 for each value written, but I itself is left unmodified.
endmodule
