// Logisim project mini_chip8_aluS.circ as structural Verilog: 4 circuits, main circuit ALU_S
module ALU_S (
  input  [7:0] VX,
  input  T1,
  input  [15:0] Input,
  input  T2,
  input  H,
  output [15:0] Output,
  output select,
  output sound,
  output END
);

  wire sound_1_select;
  wire [15:0] sound_1_output;

  CMPVS cmpvs_1 (.VX(VX), .Input(sound_1_output), .newValue(T1), .SCMPSON(sound_1_select), .Output(Output));
  Sound sound_1 (
    .Input(Input), .enable(T2), .H(H), .Output(sound_1_output), .sound(sound), .select(sound_1_select),
    .END(END));
  or or_1 (select, T1, sound_1_select);
endmodule

module CMPVS (
  input  [7:0] VX,
  input  [15:0] Input,
  input  newValue,
  input  SCMPSON,
  output [15:0] Output
);

  wire [15:0] and_1_out, and_2_out, bit_extender_1_out, bit_extender_2_out, bit_extender_3_out,
       multiplier_1_out;

  assign bit_extender_1_out = {{8{1'b0}}, VX};  // Bit_Extender bit_extender_1
  Multiplier #(.width(16)) multiplier_1 (
    .a(bit_extender_1_out), .b(16'h20), .out(multiplier_1_out), .cin({16{1'b0}}));  // open: cout
  assign bit_extender_2_out = {{15{newValue}}, newValue};  // Bit_Extender bit_extender_2
  assign bit_extender_3_out = {{15{SCMPSON}}, SCMPSON};  // Bit_Extender bit_extender_3
  assign and_1_out = multiplier_1_out & bit_extender_2_out;  // AND_Gate and_1, 16 bits wide
  assign and_2_out = Input & bit_extender_3_out;  // AND_Gate and_2, 16 bits wide
  assign Output = and_1_out | and_2_out;  // OR_Gate or_1, 16 bits wide

  // Notes on the sheet:
  //   10
endmodule

module Sound (
  input  [15:0] Input,
  input  enable,
  input  H,
  output [15:0] Output,
  output sound,
  output END,
  output select
);

  wire tmp_s_1_output;

  Comparator #(.width(16)) comparator_1 (.a(Input), .b({16{1'b0}}), .gt(sound), .eq(END));  // open: lt
  TMP_S tmp_s_1 (.enable(enable), .H(H), .Output(tmp_s_1_output));
  Subtractor #(.width(16)) subtractor_1 (.a(Input), .b(16'h1), .out(Output), .bin(1'b0));  // open: bout
  and and_1 (select, sound, tmp_s_1_output);
endmodule

module TMP_S (
  input  enable,
  input  H,
  output Output
);

  wire and_1_out, comparator_1_eq, comparator_1_lt, not_1_out;
  wire [15:0] counter_1_q;

  Counter #(.width(16), .max('hffff)) counter_1 (
    .load(1'b0), .D({16{1'b0}}), .count(enable), .Q(counter_1_q), .clk(and_1_out), .clr(not_1_out));  // open: carry
  not not_1 (not_1_out, enable);
  and and_1 (and_1_out, H, comparator_1_lt);
  Comparator #(.width(16)) comparator_1 (
    .a(counter_1_q), .b({16{1'b0}}), .eq(comparator_1_eq), .lt(comparator_1_lt));  // open: gt
  and and_2 (Output, enable, comparator_1_eq);
endmodule
