// Logisim project mini_chip8_cmpt.circ as structural Verilog: 6 circuits, main circuit ALU
module DEC (
  input  enable,
  input  [15:0] opcode,
  output _00E0,
  output _00EE,
  output _0NNN,
  output _1NNN,
  output _2NNN,
  output ANNN,
  output BNNN,
  output _3XKK,
  output _4XKK,
  output _6XKK,
  output _7XKK,
  output CXKK,
  output _5XY0,
  output _8XY0,
  output _8XY1,
  output _8XY2,
  output _8XY3,
  output _8XY4,
  output _8XY5,
  output _8XY7,
  output _9XY0,
  output DXYK,
  output _8X06,
  output _8X0E,
  output EX9E,
  output EXA1,
  output FX07,
  output FX0A,
  output FX15,
  output FX18,
  output FX1E,
  output FX29,
  output FX33,
  output FX55,
  output FX65,
  output [3:0] AX,
  output [3:0] AY,
  output [3:0] K,
  output [7:0] KK,
  output [11:0] NNN
);

  wire decop_1_p3, decop_1_p4, decop_1_p5, decop_1_p6, opx_1_p10, opx_1_p24, opxy_1_p8, opxy_1_p9, or_1_out,
       or_2_out;

  // DECOP decop_1: pin names not known; wires that end beside it: enable, opcode, decop_1_p3, decop_1_p4, decop_1_p5, decop_1_p6, decop_1_p3, decop_1_p4, decop_1_p5, decop_1_p6
  // OPNNN opnnn_1: pin names not known; wires that end beside it: _00E0, _00EE, _0NNN, _1NNN, _2NNN, ANNN, BNNN, _3XKK
  // OPXY opxy_1: pin names not known; wires that end beside it: decop_1_p3, decop_1_p4, decop_1_p5, _4XKK, _6XKK, _7XKK, CXKK, opxy_1_p8, opxy_1_p9, _5XY0, _8XY0, _8XY1, _8XY2, _8XY3, _8XY4
  // OPX opx_1: pin names not known; wires that end beside it: decop_1_p3, decop_1_p4, decop_1_p5, decop_1_p6, decop_1_p6, _8XY5, _8XY7, _9XY0, DXYK, opx_1_p10, _8X06, _8X0E, EX9E, EXA1, FX07, FX0A, FX15, FX18, FX1E, FX29, FX33, FX55, FX65, opx_1_p24
  or or_1 (or_1_out, opxy_1_p9, DXYK, opx_1_p10, opx_1_p24);
  or or_2 (or_2_out, DXYK, opx_1_p10);
  // OPDATA opdata_1: pin names not known; wires that end beside it: opcode, or_1_out, or_2_out, DXYK, opxy_1_p9, opxy_1_p8, AX, AY, K, KK, NNN
endmodule

module ALU (
  input  [3:0] X,
  input  [3:0] Y,
  input  [7:0] VX,
  input  [7:0] VY,
  input  [11:0] saut,
  input  [11:0] NNN,
  input  [11:0] PC,
  input  [3:0] nbrsaut,
  input  [7:0] KK,
  input  _0NNN,
  input  _00E0,
  input  _00EE,
  input  _1NNN,
  input  _2NNN,
  input  _3XKK,
  input  _4XKK,
  input  _5XY0,
  input  _6XKK,
  input  _7XKK,
  input  _8X06,
  input  _8X0E,
  input  _8XY0,
  input  _8XY1,
  input  _8XY2,
  input  _8XY3,
  input  _8XY4,
  input  _8XY5,
  input  _8XY7,
  input  _9XY0,
  input  ANNN,
  input  BNNN,
  input  CXKK,
  input  DXYK,
  input  EX9E,
  input  EXA1,
  input  FX07,
  input  FX0A,
  input  FX15,
  input  FX18,
  input  FX1E,
  input  FX29,
  input  FX33,
  input  FX55,
  input  FX65,
  input  [15:0] CMPSON,
  input  SCP,
  input  [3:0] K,
  input  [7:0] CMPGAME,
  input  [7:0] V0,
  input  [4:0] CL,
  input  [11:0] I,
  input  [7:0] DR,
  input  H,
  input  T1,
  input  T2,
  output RE,
  output Snbrsaut,
  output [3:0] nbrsaut_2,
  output [11:0] saut_2,
  output Ssaut,
  output [7:0] VF,
  output SVF,
  output [3:0] AY,
  output [11:0] PC_2,
  output SPC,
  output [11:0] I_2,
  output SI,
  output [11:0] AR,
  output [5:0] SCX,
  output [4:0] SCY,
  output SCstore,
  output SSCP,
  output [7:0] CMPGAME_2,
  output SCMPGAME,
  output [15:0] CMPSON_2,
  output SCMPSON,
  output [7:0] DR_2,
  output SR,
  output [7:0] VX_2,
  output SVX,
  output [3:0] AX,
  output EC,
  output [3:0] NC,
  output SON
);

  wire alu1_1_p25, alu1_1_p33, alu1_1_p34, alu2_1_ec, alu2_1_svf, alu2_1_svx, alu3_1_ec, alu3_1_si,
       alu3_1_spc, alu3_1_svf, alu3_1_svx, alu4_1_p25, alu4_1_p27, alu4_1_p32, alu4_1_p34;
  wire [3:0] alu1_1_p30, alu1_1_p31, alu1_1_p35, alu2_1_ax, alu2_1_ay, alu2_1_nc, alu3_1_ax, alu3_1_ay,
       alu3_1_nc, alu4_1_p33, alu4_1_p35;
  wire [7:0] alu1_1_p32, alu2_1_vf, alu2_1_vx_2, alu3_1_df, alu3_1_vx_2, alu4_1_p24, alu4_1_p31;
  wire [11:0] alu1_1_p24, alu3_1_ar, alu3_1_i_2, alu3_1_pc_2, alu4_1_p26, alu4_1_p30;

  // ALU1 alu1_1: pin names not known; wires that end beside it: saut, NNN, PC, nbrsaut, X, VX, KK, Y, VY, _0NNN, _00E0, _00EE, _1NNN, _2NNN, _3XKK, _4XKK, _5XY0, _6XKK, _7XKK, T1, T2, H, RE, alu1_1_p24, alu1_1_p25, Snbrsaut, nbrsaut_2, saut_2, Ssaut, alu1_1_p30, alu1_1_p31, alu1_1_p32, alu1_1_p33, alu1_1_p34, alu1_1_p35
  ALU2 alu2_1 (
    .X(X), .VX(VX), .Y(Y), .VY(VY), ._8X06(_8X06), ._8X0E(_8X0E), ._8XY0(_8XY0), ._8XY1(_8XY1),
    ._8XY2(_8XY2), ._8XY3(_8XY3), ._8XY4(_8XY4), ._8XY5(_8XY5), ._8XY7(_8XY7), .T1(T1), .AY(alu2_1_ay),
    .VF(alu2_1_vf), .SVF(alu2_1_svf), .AX(alu2_1_ax), .VX_2(alu2_1_vx_2), .SVX(alu2_1_svx), .EC(alu2_1_ec),
    .NC(alu2_1_nc), .H(H));
  ALU3 alu3_1 (
    .Y(Y), .X(X), .VX(VX), .VY(VY), .PC(PC), .NNN(NNN), .V0(V0), .KK(KK), .I(I), .DR(DR), .SCP(SCP), .K(K),
    ._9XY0(_9XY0), .ANNN(ANNN), .BNNN(BNNN), .CXKK(CXKK), .DXYK(DXYK), .EX9E(EX9E), .EXA1(EXA1), .CL(CL),
    .T1(T1), .T2(T2), .H(H), .I_2(alu3_1_i_2), .SI(alu3_1_si), .VX_2(alu3_1_vx_2), .SVX(alu3_1_svx),
    .DF(alu3_1_df), .SVF(alu3_1_svf), .SCX(SCX), .SCY(SCY), .AR(alu3_1_ar), .SCstore(SCstore), .SSCP(SSCP),
    .AY(alu3_1_ay), .PC_2(alu3_1_pc_2), .SPC(alu3_1_spc), .AX(alu3_1_ax), .EC(alu3_1_ec), .NC(alu3_1_nc));
  // ALU4 alu4_1: pin names not known; wires that end beside it: X, CMPGAME, CL, VX, I, DR, FX07, FX0A, FX15, FX18, FX1E, FX29, FX33, FX55, FX65, H, T1, T2, CMPSON, CMPGAME_2, SCMPGAME, CMPSON_2, SCMPSON, alu4_1_p24, alu4_1_p25, alu4_1_p26, alu4_1_p27, DR_2, SR, alu4_1_p30, alu4_1_p31, alu4_1_p32, alu4_1_p33, alu4_1_p34, alu4_1_p35, SON
  assign VX_2 = alu1_1_p32 | alu2_1_vx_2 | alu3_1_vx_2 | alu4_1_p31;  // OR_Gate or_1, 8 bits wide
  or or_2 (SVX, alu1_1_p33, alu2_1_svx, alu3_1_svx, alu4_1_p32);
  assign AX = alu1_1_p30 | alu2_1_ax | alu3_1_ax | alu4_1_p33;  // OR_Gate or_3, 4 bits wide
  or or_4 (EC, alu1_1_p34, alu2_1_ec, alu3_1_ec, alu4_1_p34);
  assign NC = alu1_1_p35 | alu2_1_nc | alu3_1_nc | alu4_1_p35;  // OR_Gate or_5, 4 bits wide
  assign VF = alu2_1_vf | alu3_1_df | alu4_1_p24;  // OR_Gate or_6, 8 bits wide
  or or_7 (SVF, alu2_1_svf, alu3_1_svf, alu4_1_p25);
  assign AY = alu1_1_p31 | alu2_1_ay | alu3_1_ay;  // OR_Gate or_8, 4 bits wide
  assign PC_2 = alu1_1_p24 | alu3_1_pc_2;  // OR_Gate or_9, 12 bits wide
  or or_10 (SPC, alu1_1_p25, alu3_1_spc);
  assign I_2 = alu3_1_i_2 | alu4_1_p26;  // OR_Gate or_11, 12 bits wide
  or or_12 (SI, alu3_1_si, alu4_1_p27);
  assign AR = alu3_1_ar | alu4_1_p30;  // OR_Gate or_13, 12 bits wide
endmodule

module CPM (
  input  enable,
  input  H,
  input  [3:0] NC,
  input  EC,
  output T0,
  output T1,
  output T2,
  output T3,
  output T4,
  output T5,
  output T6,
  output T7,
  output \end 
);

  wire and_1_out, and_2_out, and_3_out, comparator_1_eq, comparator_2_gt, comparator_2_lt, not_1_out,
       not_2_out, or_1_out;
  wire [3:0] counter_1_q;

  not not_1 (not_1_out, enable);
  and and_1 (and_1_out, H, and_3_out);
  and and_2 (and_2_out, enable, and_3_out);
  Counter #(.width(4), .max('hf)) counter_1 (
    .load(1'b0), .D(4'b0000), .count(and_2_out), .Q(counter_1_q), .clk(and_1_out), .clr(not_1_out));  // open: carry
  Decoder #(.select(3), .disabled(0)) decoder_1 (
    .out0(T0), .out1(T1), .out2(T2), .out3(T3), .out4(T4), .out5(T5), .out6(T6), .out7(T7),
    .sel(counter_1_q[2:0]), .en(enable));
  Comparator #(.width(4)) comparator_1 (.a(counter_1_q), .b(NC), .eq(comparator_1_eq));  // open: gt, lt
  not not_2 (not_2_out, comparator_1_eq);
  and and_3 (and_3_out, not_2_out, EC);
  Comparator #(.width(4)) comparator_2 (
    .a(counter_1_q), .b(4'b0000), .gt(comparator_2_gt), .lt(comparator_2_lt));  // open: eq
  or or_1 (or_1_out, comparator_2_gt, comparator_2_lt);
  and and_4 (\end , comparator_1_eq, or_1_out, enable);
endmodule

module loadR (
  input  [7:0] DR,
  input  enable,
  input  H,
  input  clear,
  input  [11:0] PC,
  output [15:0] opcode,
  output \end ,
  output SPC,
  output [11:0] PC_2
);

  wire and_1_out, and_4_out, and_6_out, not_1_out, not_2_out, not_3_out;
  wire [1:0] counter_1_q;
  wire [7:0] and_2_out, and_3_out, bit_extender_1_out, bit_extender_2_out, register_1_q;
  wire [11:0] adder_1_out, bit_extender_3_out;

  assign bit_extender_1_out = {{7{and_6_out}}, and_6_out};  // Bit_Extender bit_extender_1
  assign bit_extender_2_out = {{7{and_4_out}}, and_4_out};  // Bit_Extender bit_extender_2
  and and_1 (and_1_out, H, enable, not_1_out);
  assign and_2_out = bit_extender_1_out & DR;  // AND_Gate and_2, 8 bits wide
  assign and_3_out = DR & bit_extender_2_out;  // AND_Gate and_3, 8 bits wide
  Counter #(.width(2), .max('h3)) counter_1 (
    .load(1'b0), .D(2'b00), .count(enable), .Q(counter_1_q), .clk(and_1_out), .clr(clear));  // open: carry
  not not_1 (not_1_out, \end );
  or or_1 (SPC, and_4_out, and_6_out);
  Adder #(.width(12)) adder_1 (.a(PC), .b(12'h1), .out(adder_1_out), .cin(1'b0));  // open: cout
  Register register_1 (.D(and_3_out), .en(and_4_out), .Q(register_1_q), .clk(and_1_out), .clr(clear));
  and and_4 (and_4_out, counter_1_q[0], not_2_out);
  not not_2 (not_2_out, counter_1_q[1]);
  Comparator #(.width(2)) comparator_1 (.a(counter_1_q), .b(2'b11), .eq(\end ));  // open: gt, lt
  assign bit_extender_3_out = {{11{SPC}}, SPC};  // Bit_Extender bit_extender_3
  Register #(.width(16)) register_2 (
    .D({register_1_q, and_2_out}), .en(and_6_out), .Q(opcode), .clk(and_1_out), .clr(clear));
  not not_3 (not_3_out, counter_1_q[0]);
  assign PC_2 = adder_1_out & bit_extender_3_out;  // AND_Gate and_5, 12 bits wide
  and and_6 (and_6_out, not_3_out, counter_1_q[1]);
endmodule

module REGI_DB (
  input  [7:0] DE,
  input  [3:0] AX,
  input  [3:0] AY,
  input  H,
  input  storeX,
  input  loadX,
  input  loadY,
  input  select,
  input  clear,
  input  [7:0] EDF,
  input  storeF,
  output [7:0] D0,
  output [31:0] R0_3,
  output [7:0] DX,
  output [31:0] R4_7,
  output [7:0] DY,
  output [31:0] R8_B,
  output [31:0] RC_F
);

  wire and_1_out, and_2_out, and_3_out, and_6_out, and_7_out, demultiplexer_2_out0, demultiplexer_2_out1,
       demultiplexer_2_out2, demultiplexer_2_out3, demultiplexer_2_out4, demultiplexer_2_out5,
       demultiplexer_2_out6, demultiplexer_2_out7, demultiplexer_2_out8, demultiplexer_2_out9,
       demultiplexer_2_out10, demultiplexer_2_out11, demultiplexer_2_out12, demultiplexer_2_out13,
       demultiplexer_2_out14, demultiplexer_2_out15, not_2_out, or_2_out;
  wire [7:0] and_4_out, and_5_out, bit_extender_1_out, demultiplexer_1_out0, demultiplexer_1_out1,
       demultiplexer_1_out2, demultiplexer_1_out3, demultiplexer_1_out4, demultiplexer_1_out5,
       demultiplexer_1_out6, demultiplexer_1_out7, demultiplexer_1_out8, demultiplexer_1_out9,
       demultiplexer_1_out10, demultiplexer_1_out11, demultiplexer_1_out12, demultiplexer_1_out13,
       demultiplexer_1_out14, demultiplexer_1_out15, not_1_out, or_1_out;

  and and_1 (and_1_out, storeX, select);
  and and_2 (and_2_out, loadX, select);
  and and_3 (and_3_out, loadY, select);
  Demultiplexer #(.select(4), .width(8), .disabled(0)) demultiplexer_1 (
    .out0(demultiplexer_1_out0), .out1(demultiplexer_1_out1), .out2(demultiplexer_1_out2),
    .out3(demultiplexer_1_out3), .out4(demultiplexer_1_out4), .out5(demultiplexer_1_out5),
    .out6(demultiplexer_1_out6), .out7(demultiplexer_1_out7), .out8(demultiplexer_1_out8),
    .out9(demultiplexer_1_out9), .out10(demultiplexer_1_out10), .out11(demultiplexer_1_out11),
    .out12(demultiplexer_1_out12), .out13(demultiplexer_1_out13), .out14(demultiplexer_1_out14),
    .out15(demultiplexer_1_out15), .in(DE), .sel(AX), .en(and_1_out));
  Demultiplexer #(.select(4), .disabled(0)) demultiplexer_2 (
    .out0(demultiplexer_2_out0), .out1(demultiplexer_2_out1), .out2(demultiplexer_2_out2),
    .out3(demultiplexer_2_out3), .out4(demultiplexer_2_out4), .out5(demultiplexer_2_out5),
    .out6(demultiplexer_2_out6), .out7(demultiplexer_2_out7), .out8(demultiplexer_2_out8),
    .out9(demultiplexer_2_out9), .out10(demultiplexer_2_out10), .out11(demultiplexer_2_out11),
    .out12(demultiplexer_2_out12), .out13(demultiplexer_2_out13), .out14(demultiplexer_2_out14),
    .out15(demultiplexer_2_out15), .in(H), .sel(AX), .en(and_1_out));
  assign bit_extender_1_out = {{7{storeF}}, storeF};  // Bit_Extender bit_extender_1
  assign not_1_out = ~bit_extender_1_out;  // NOT_Gate not_1, 8 bits wide
  assign and_4_out = EDF & bit_extender_1_out;  // AND_Gate and_4, 8 bits wide
  assign and_5_out = demultiplexer_1_out15 & not_1_out;  // AND_Gate and_5, 8 bits wide
  assign or_1_out = and_5_out | and_4_out;  // OR_Gate or_1, 8 bits wide
  not not_2 (not_2_out, storeF);
  and and_6 (and_6_out, demultiplexer_2_out15, not_2_out);
  and and_7 (and_7_out, storeF, H);
  or or_2 (or_2_out, and_6_out, and_7_out);
  Register register_1 (.D(demultiplexer_1_out0), .en(select), .Q(D0), .clk(demultiplexer_2_out0), .clr(clear));
  Register register_2 (.D(demultiplexer_1_out1), .en(select), .Q(R0_3[15:8]), .clk(demultiplexer_2_out1), .clr(clear));
  Register register_3 (.D(demultiplexer_1_out2), .en(select), .Q(R0_3[23:16]), .clk(demultiplexer_2_out2), .clr(clear));
  Register register_4 (.D(demultiplexer_1_out3), .en(select), .Q(R0_3[31:24]), .clk(demultiplexer_2_out3), .clr(clear));
  Register register_5 (.D(demultiplexer_1_out4), .en(select), .Q(R4_7[7:0]), .clk(demultiplexer_2_out4), .clr(clear));
  Register register_6 (.D(demultiplexer_1_out5), .en(select), .Q(R4_7[15:8]), .clk(demultiplexer_2_out5), .clr(clear));
  Register register_7 (.D(demultiplexer_1_out6), .en(select), .Q(R4_7[23:16]), .clk(demultiplexer_2_out6), .clr(clear));
  Register register_8 (.D(demultiplexer_1_out7), .en(select), .Q(R4_7[31:24]), .clk(demultiplexer_2_out7), .clr(clear));
  Register register_9 (.D(demultiplexer_1_out8), .en(select), .Q(R8_B[7:0]), .clk(demultiplexer_2_out8), .clr(clear));
  Register register_10 (.D(demultiplexer_1_out9), .en(select), .Q(R8_B[15:8]), .clk(demultiplexer_2_out9), .clr(clear));
  Register register_11 (
    .D(demultiplexer_1_out10), .en(select), .Q(R8_B[23:16]), .clk(demultiplexer_2_out10), .clr(clear));
  Register register_12 (
    .D(demultiplexer_1_out11), .en(select), .Q(R8_B[31:24]), .clk(demultiplexer_2_out11), .clr(clear));
  Register register_13 (
    .D(demultiplexer_1_out12), .en(select), .Q(RC_F[7:0]), .clk(demultiplexer_2_out12), .clr(clear));
  Register register_14 (
    .D(demultiplexer_1_out13), .en(select), .Q(RC_F[15:8]), .clk(demultiplexer_2_out13), .clr(clear));
  Register register_15 (
    .D(demultiplexer_1_out14), .en(select), .Q(RC_F[23:16]), .clk(demultiplexer_2_out14), .clr(clear));
  Register register_16 (.D(or_1_out), .en(select), .Q(RC_F[31:24]), .clk(or_2_out), .clr(clear));
  Multiplexer #(.select(4), .width(8), .disabled(0)) multiplexer_1 (
    .in0(D0), .in1(R0_3[15:8]), .in2(R0_3[23:16]), .in3(R0_3[31:24]), .in4(R4_7[7:0]), .in5(R4_7[15:8]),
    .in6(R4_7[23:16]), .in7(R4_7[31:24]), .in8(R8_B[7:0]), .in9(R8_B[15:8]), .in10(R8_B[23:16]),
    .in11(R8_B[31:24]), .in12(RC_F[7:0]), .in13(RC_F[15:8]), .in14(RC_F[23:16]), .in15(RC_F[31:24]),
    .out(DX), .sel(AX), .en(and_2_out));
  Multiplexer #(.select(4), .width(8), .disabled(0)) multiplexer_2 (
    .in0(D0), .in1(R0_3[15:8]), .in2(R0_3[23:16]), .in3(R0_3[31:24]), .in4(R4_7[7:0]), .in5(R4_7[15:8]),
    .in6(R4_7[23:16]), .in7(R4_7[31:24]), .in8(R8_B[7:0]), .in9(R8_B[15:8]), .in10(R8_B[23:16]),
    .in11(R8_B[31:24]), .in12(RC_F[7:0]), .in13(RC_F[15:8]), .in14(RC_F[23:16]), .in15(RC_F[31:24]),
    .out(DY), .sel(AY), .en(and_3_out));

  assign R0_3[7:0] = D0;
endmodule

module MA (
  input  MA,
  input  RESET,
  output LedM,
  output MA_2,
  output R
);

  wire d_ff_1_qn, not_1_out;

  or or_1 (R, not_1_out, RESET);
  D_Flip_Flop d_ff_1 (.clk(MA), .D(d_ff_1_qn), .Q(LedM), .Qn(d_ff_1_qn), .preset(1'b0), .en(1'b1), .reset(1'b0));
  not not_1 (not_1_out, LedM);

  assign MA_2 = LedM;

  // Notes on the sheet:
  //   MARCHE / ARRET
endmodule
