// Logisim project other_chip8_lib.circ as structural Verilog: 15 circuits, main circuit COD4+
module COD4 (
  input  Input_0,
  input  Input_1,
  input  Input_2,
  input  Input_3,
  input  Enable,
  output Error,
  output Validate,
  output [1:0] Output
);

  wire nor_1_out, or_1_out, or_2_out, or_3_out;

  nor nor_1 (nor_1_out, Input_1, Input_0, Input_2, Input_3);
  or or_1 (or_1_out, Input_0, Input_1, Input_2, Input_3);
  or or_2 (or_2_out, Input_1, Input_3);
  or or_3 (or_3_out, Input_3, Input_2);
  and and_1 (Error, nor_1_out, Enable);
  and and_2 (Validate, or_1_out, Enable);
  and and_3 (Output[0], or_2_out, Enable);
  and and_4 (Output[1], or_3_out, Enable);
endmodule

module COD4_2 (
  input  Input_0,
  input  Input_1,
  input  Input_2,
  input  Input_3,
  input  Enable,
  output Validate,
  output Error,
  output [1:0] Output
);

  wire and_1_out, and_2_out, and_3_out, not_1_out, not_2_out, not_3_out;

  not not_1 (not_1_out, Input_1);
  not not_2 (not_2_out, Input_2);
  not not_3 (not_3_out, Input_3);
  and and_1 (and_1_out, Input_0, not_1_out, not_2_out, not_3_out);
  and and_2 (and_2_out, Input_1, not_2_out, not_3_out);
  and and_3 (and_3_out, Input_2, not_3_out);
  COD4 cod4_1 (
    .Input_0(and_1_out), .Input_1(and_2_out), .Input_2(and_3_out), .Input_3(Input_3), .Enable(Enable),
    .Validate(Validate), .Output(Output), .Error(Error));
endmodule

module COD8 (
  input  Input_0,
  input  Input_1,
  input  Input_2,
  input  Input_3,
  input  Input_4,
  input  Input_5,
  input  Input_6,
  input  Input_7,
  input  Enable,
  output Error,
  output Validate,
  output [2:0] Output
);

  wire and_2_out, cod4_1_error, cod4_1_validate, cod4_2_error, not_1_out;
  wire [1:0] cod4_1_output, cod4_2_output;

  COD4_2 cod4_1 (
    .Enable(and_2_out), .Output(cod4_1_output), .Validate(cod4_1_validate), .Input_0(Input_0),
    .Input_1(Input_1), .Input_2(Input_2), .Input_3(Input_3), .Error(cod4_1_error));
  COD4_2 cod4_2 (
    .Enable(Enable), .Output(cod4_2_output), .Validate(Output[2]), .Input_0(Input_4), .Input_1(Input_5),
    .Input_2(Input_6), .Input_3(Input_7), .Error(cod4_2_error));
  and and_1 (Error, cod4_1_error, cod4_2_error);
  or or_1 (Validate, cod4_1_validate, Output[2]);
  assign Output[1:0] = cod4_1_output | cod4_2_output;  // OR_Gate or_2, 2 bits wide
  not not_1 (not_1_out, Output[2]);
  and and_2 (and_2_out, not_1_out, Enable);
endmodule

module COD4_2_2 (
  input  Input_3,
  input  Input_2,
  input  Input_1,
  input  Input_0,
  input  Enable,
  output Validate,
  output Error,
  output [1:0] Output
);

  wire not_1_out, not_2_out, not_3_out;
  wire [2:0] and_1_out;

  not not_1 (not_1_out, Input_2);
  not not_2 (not_2_out, Input_1);
  not not_3 (not_3_out, Input_0);
  and and_1 (and_1_out[0], Input_3, not_1_out, not_2_out, not_3_out);
  and and_2 (and_1_out[1], Input_2, not_2_out, not_3_out);
  and and_3 (and_1_out[2], Input_1, not_3_out);
  COD4 cod4_1 (
    .Input_0(Input_0), .Input_1(and_1_out[2]), .Input_2(and_1_out[1]), .Input_3(and_1_out[0]),
    .Enable(Enable), .Validate(Validate), .Output(Output), .Error(Error));
endmodule

module COD8_2 (
  input  Enable,
  input  Input_0,
  input  Input_1,
  input  Input_2,
  input  Input_3,
  input  Input_4,
  input  Input_5,
  input  Input_6,
  input  Input_7,
  output Error,
  output [2:0] Output,
  output Validate
);

  wire and_2_out, cod4_1_error, cod4_1_validate, cod4_2_error, cod4_2_validate, not_1_out;
  wire [1:0] cod4_1_output, cod4_2_output;

  COD4_2_2 cod4_1 (
    .Input_3(Input_3), .Input_2(Input_2), .Input_1(Input_1), .Input_0(Input_0), .Enable(Enable),
    .Validate(cod4_1_validate), .Output(cod4_1_output), .Error(cod4_1_error));
  COD4_2_2 cod4_2 (
    .Input_3(Input_7), .Input_2(Input_6), .Input_1(Input_5), .Input_0(Input_4), .Enable(and_2_out),
    .Validate(cod4_2_validate), .Output(cod4_2_output), .Error(cod4_2_error));
  and and_1 (Error, cod4_1_error, cod4_2_error);
  not not_1 (not_1_out, cod4_1_validate);
  and and_2 (and_2_out, Enable, not_1_out);
  and and_3 (Output[2], and_2_out, cod4_2_validate);
  assign Output[1:0] = cod4_1_output | cod4_2_output;  // OR_Gate or_1, 2 bits wide
  or or_2 (Validate, cod4_2_validate, cod4_1_validate);
endmodule

module L32 (
  input  E,
  input  [4:0] L,
  input  I,
  input  H,
  input  CL,
  output [31:0] O
);

  wire [31:0] and_1_out, and_2_out, bit_extender_1_out, decoder_1_out31, not_1_out, or_1_out;

  Decoder #(.select(5), .disabled(0)) decoder_1 (
    .out0(decoder_1_out31[31]), .out1(decoder_1_out31[30]), .out2(decoder_1_out31[29]),
    .out3(decoder_1_out31[28]), .out4(decoder_1_out31[27]), .out5(decoder_1_out31[26]),
    .out6(decoder_1_out31[25]), .out7(decoder_1_out31[24]), .out8(decoder_1_out31[23]),
    .out9(decoder_1_out31[22]), .out10(decoder_1_out31[21]), .out11(decoder_1_out31[20]),
    .out12(decoder_1_out31[19]), .out13(decoder_1_out31[18]), .out14(decoder_1_out31[17]),
    .out15(decoder_1_out31[16]), .out16(decoder_1_out31[15]), .out17(decoder_1_out31[14]),
    .out18(decoder_1_out31[13]), .out19(decoder_1_out31[12]), .out20(decoder_1_out31[11]),
    .out21(decoder_1_out31[10]), .out22(decoder_1_out31[9]), .out23(decoder_1_out31[8]),
    .out24(decoder_1_out31[7]), .out25(decoder_1_out31[6]), .out26(decoder_1_out31[5]),
    .out27(decoder_1_out31[4]), .out28(decoder_1_out31[3]), .out29(decoder_1_out31[2]),
    .out30(decoder_1_out31[1]), .out31(decoder_1_out31[0]), .sel(L), .en(E));
  assign not_1_out = ~decoder_1_out31;  // NOT_Gate not_1, 32 bits wide
  assign bit_extender_1_out = {{31{I}}, I};  // Bit_Extender bit_extender_1
  assign and_1_out = not_1_out & O;  // AND_Gate and_1, 32 bits wide
  assign and_2_out = bit_extender_1_out & decoder_1_out31;  // AND_Gate and_2, 32 bits wide
  assign or_1_out = and_1_out | and_2_out;  // OR_Gate or_1, 32 bits wide
  Register #(.width(32)) register_1 (.D(or_1_out), .en(E), .Q(O), .clk(H), .clr(CL));

  // Notes on the sheet:
  //   L: pull=down
endmodule

module LC8 (
  input  Enable,
  input  [2:0] X,
  input  [4:0] Y,
  input  I,
  input  H,
  input  CL,
  output [31:0] O0,
  output [31:0] O1,
  output [31:0] O2,
  output [31:0] O3,
  output [31:0] O4,
  output [31:0] O5,
  output [31:0] O6,
  output [31:0] O7
);

  wire decoder_1_out0, decoder_1_out1, decoder_1_out2, decoder_1_out3, decoder_1_out4, decoder_1_out5,
       decoder_1_out6, decoder_1_out7;

  Decoder #(.select(3), .disabled(0)) decoder_1 (
    .out0(decoder_1_out0), .out1(decoder_1_out1), .out2(decoder_1_out2), .out3(decoder_1_out3),
    .out4(decoder_1_out4), .out5(decoder_1_out5), .out6(decoder_1_out6), .out7(decoder_1_out7), .sel(X),
    .en(Enable));
  L32 l32_1 (.E(decoder_1_out0), .L(Y), .I(I), .H(H), .CL(CL), .O(O0));
  L32 l32_2 (.E(decoder_1_out1), .L(Y), .I(I), .H(H), .CL(CL), .O(O1));
  L32 l32_3 (.E(decoder_1_out2), .L(Y), .I(I), .H(H), .CL(CL), .O(O2));
  L32 l32_4 (.E(decoder_1_out3), .L(Y), .I(I), .H(H), .CL(CL), .O(O3));
  L32 l32_5 (.E(decoder_1_out4), .L(Y), .I(I), .H(H), .CL(CL), .O(O4));
  L32 l32_6 (.E(decoder_1_out5), .L(Y), .I(I), .H(H), .CL(CL), .O(O5));
  L32 l32_7 (.E(decoder_1_out6), .L(Y), .I(I), .H(H), .CL(CL), .O(O6));
  L32 l32_8 (.E(decoder_1_out7), .L(Y), .I(I), .H(H), .CL(CL), .O(O7));
endmodule

module LC32 (
  input  enable,
  input  [4:0] X,
  input  [4:0] Y,
  input  H,
  input  I,
  input  C,
  output [31:0] O0,
  output [31:0] out_8,
  output [31:0] out_9,
  output [31:0] out_10,
  output [31:0] out_11,
  output [31:0] out_12,
  output [31:0] out_13,
  output [31:0] out_14,
  output [31:0] out_15,
  output [31:0] out_16,
  output [31:0] out_17,
  output [31:0] out_18,
  output [31:0] out_19,
  output [31:0] out_20,
  output [31:0] out_21,
  output [31:0] out_22,
  output [31:0] out_23,
  output [31:0] out_24,
  output [31:0] out_25,
  output [31:0] out_26,
  output [31:0] out_27,
  output [31:0] out_28,
  output [31:0] out_29,
  output [31:0] out_30,
  output [31:0] out_31,
  output [31:0] out_32,
  output [31:0] out_33,
  output [31:0] out_34,
  output [31:0] out_35,
  output [31:0] out_36,
  output [31:0] out_37,
  output [31:0] out_38
);

  wire decoder_1_out0, decoder_1_out1, decoder_1_out2, decoder_1_out3;

  Decoder #(.select(2), .disabled(0)) decoder_1 (
    .out0(decoder_1_out0), .out1(decoder_1_out1), .out2(decoder_1_out2), .out3(decoder_1_out3), .sel(X[4:3]),
    .en(enable));
  LC8 lc8_1 (
    .Enable(decoder_1_out0), .X(X[2:0]), .Y(Y), .I(I), .H(H), .CL(C), .O0(O0), .O1(out_8), .O2(out_9),
    .O3(out_10), .O4(out_11), .O5(out_12), .O6(out_13), .O7(out_14));
  LC8 lc8_2 (
    .Enable(decoder_1_out1), .X(X[2:0]), .Y(Y), .I(I), .H(H), .CL(C), .O0(out_15), .O1(out_16), .O2(out_17),
    .O3(out_18), .O4(out_19), .O5(out_20), .O6(out_21), .O7(out_22));
  LC8 lc8_3 (
    .Enable(decoder_1_out2), .X(X[2:0]), .Y(Y), .I(I), .H(H), .CL(C), .O0(out_23), .O1(out_24), .O2(out_25),
    .O3(out_26), .O4(out_27), .O5(out_28), .O6(out_29), .O7(out_30));
  LC8 lc8_4 (
    .Enable(decoder_1_out3), .X(X[2:0]), .Y(Y), .I(I), .H(H), .CL(C), .O0(out_31), .O1(out_32), .O2(out_33),
    .O3(out_34), .O4(out_35), .O5(out_36), .O6(out_37), .O7(out_38));
endmodule

module COL32 (
  input  Enable,
  input  [4:0] L,
  input  Input,
  input  H,
  input  Clear,
  output Output
);

  wire [31:0] l32_1_o;

  L32 l32_1 (.E(Enable), .L(L), .I(Input), .H(H), .CL(Clear), .O(l32_1_o));
  Multiplexer #(.select(5), .disabled(0), .enable("false")) multiplexer_1 (
    .in0(l32_1_o[31]), .in1(l32_1_o[30]), .in2(l32_1_o[29]), .in3(l32_1_o[28]), .in4(l32_1_o[27]),
    .in5(l32_1_o[26]), .in6(l32_1_o[25]), .in7(l32_1_o[24]), .in8(l32_1_o[23]), .in9(l32_1_o[22]),
    .in10(l32_1_o[21]), .in11(l32_1_o[20]), .in12(l32_1_o[19]), .in13(l32_1_o[18]), .in14(l32_1_o[17]),
    .in15(l32_1_o[16]), .in16(l32_1_o[15]), .in17(l32_1_o[14]), .in18(l32_1_o[13]), .in19(l32_1_o[12]),
    .in20(l32_1_o[11]), .in21(l32_1_o[10]), .in22(l32_1_o[9]), .in23(l32_1_o[8]), .in24(l32_1_o[7]),
    .in25(l32_1_o[6]), .in26(l32_1_o[5]), .in27(l32_1_o[4]), .in28(l32_1_o[3]), .in29(l32_1_o[2]),
    .in30(l32_1_o[1]), .in31(l32_1_o[0]), .out(Output), .sel(L));
endmodule

module COLC8 (
  input  Enable,
  input  [2:0] X,
  input  [4:0] Y,
  input  I,
  input  H,
  input  CL,
  output OS
);

  wire col32_1_output, col32_2_output, col32_3_output, col32_4_output, col32_5_output, col32_6_output,
       col32_7_output, col32_8_output, decoder_1_out0, decoder_1_out1, decoder_1_out2, decoder_1_out3,
       decoder_1_out4, decoder_1_out5, decoder_1_out6, decoder_1_out7;

  Decoder #(.select(3), .disabled(0)) decoder_1 (
    .out0(decoder_1_out0), .out1(decoder_1_out1), .out2(decoder_1_out2), .out3(decoder_1_out3),
    .out4(decoder_1_out4), .out5(decoder_1_out5), .out6(decoder_1_out6), .out7(decoder_1_out7), .sel(X),
    .en(Enable));
  COL32 col32_1 (.Enable(decoder_1_out0), .L(Y), .Input(I), .H(H), .Clear(CL), .Output(col32_1_output));
  COL32 col32_2 (.Enable(decoder_1_out1), .L(Y), .Input(I), .H(H), .Clear(CL), .Output(col32_2_output));
  COL32 col32_3 (.Enable(decoder_1_out2), .L(Y), .Input(I), .H(H), .Clear(CL), .Output(col32_3_output));
  COL32 col32_4 (.Enable(decoder_1_out3), .L(Y), .Input(I), .H(H), .Clear(CL), .Output(col32_4_output));
  COL32 col32_5 (.Enable(decoder_1_out4), .L(Y), .Input(I), .H(H), .Clear(CL), .Output(col32_5_output));
  COL32 col32_6 (.Enable(decoder_1_out5), .L(Y), .Input(I), .H(H), .Clear(CL), .Output(col32_6_output));
  COL32 col32_7 (.Enable(decoder_1_out6), .L(Y), .Input(I), .H(H), .Clear(CL), .Output(col32_7_output));
  COL32 col32_8 (.Enable(decoder_1_out7), .L(Y), .Input(I), .H(H), .Clear(CL), .Output(col32_8_output));
  Multiplexer #(.select(3), .enable("false")) multiplexer_1 (
    .in0(col32_1_output), .in1(col32_2_output), .in2(col32_3_output), .in3(col32_4_output),
    .in4(col32_5_output), .in5(col32_6_output), .in6(col32_7_output), .in7(col32_8_output), .out(OS), .sel(X));
endmodule

module IGRC (
  input  [23:0] I,
  input  CL,
  input  H,
  output [5:0] OX,
  output [4:0] OY,
  output IGD,
  output [23:0] OC,
  output [11:0] AR
);

  wire and_1_out, comparator_1_eq, comparator_1_gt, comparator_1_lt, comparator_2_lt, d_ff_1_q;
  wire [4:0] bit_extender_5_out, bit_extender_7_out;
  wire [5:0] bit_extender_4_out, bit_extender_6_out;
  wire [12:0] bit_extender_1_out, bit_extender_2_out, counter_1_q, divider_1_out, divider_1_rem,
       subtractor_1_out;
  wire [23:0] bit_extender_8_out, register_1_q, register_2_q;

  and and_1 (and_1_out, H, d_ff_1_q);
  Register #(.width(24)) register_1 (.D(I), .en(comparator_1_lt), .Q(register_1_q), .clk(and_1_out), .clr(CL));
  Register #(.width(24)) register_2 (.D(I), .en(comparator_1_eq), .Q(register_2_q), .clk(and_1_out), .clr(CL));
  Subtractor #(.width(13)) subtractor_1 (.a(counter_1_q), .b(13'h2), .out(subtractor_1_out), .bin(1'b0));  // open: bout
  Bit_Extender #(.in_width(24), .out_width(13)) bit_extender_1 (.in(register_1_q), .out(bit_extender_1_out));
  Bit_Extender #(.in_width(24), .out_width(13)) bit_extender_2 (.in(register_2_q), .out(bit_extender_2_out));
  Divider #(.width(13)) divider_1 (
    .a(subtractor_1_out), .b(bit_extender_2_out), .out(divider_1_out), .rem(divider_1_rem));  // open: upper
  Comparator #(.width(13)) comparator_1 (
    .a(counter_1_q), .b(13'h1), .gt(comparator_1_gt), .eq(comparator_1_eq), .lt(comparator_1_lt));
  Counter #(.width(13), .max('h1fff), .ongoal("stay")) counter_1 (
    .load(1'b0), .D({13{1'b0}}), .count(1'b1), .Q(counter_1_q), .clk(and_1_out), .clr(CL));  // open: carry
  Bit_Extender #(.in_width(13), .out_width(12)) bit_extender_3 (.in(counter_1_q), .out(AR));
  Bit_Extender #(.in_width(13), .out_width(6)) bit_extender_4 (.in(divider_1_out), .out(bit_extender_4_out));
  Bit_Extender #(.in_width(13), .out_width(5)) bit_extender_5 (.in(divider_1_rem), .out(bit_extender_5_out));
  Comparator #(.width(13)) comparator_2 (
    .a(divider_1_out), .b(bit_extender_1_out), .lt(comparator_2_lt));  // open: gt, eq
  assign OX = bit_extender_4_out & bit_extender_6_out;  // AND_Gate and_2, 6 bits wide
  assign bit_extender_6_out = {{5{comparator_1_gt}}, comparator_1_gt};  // Bit_Extender bit_extender_6
  assign OY = bit_extender_5_out & bit_extender_7_out;  // AND_Gate and_3, 5 bits wide
  assign bit_extender_7_out = {{4{comparator_1_gt}}, comparator_1_gt};  // Bit_Extender bit_extender_7
  D_Flip_Flop d_ff_1 (.clk(H), .D(comparator_2_lt), .Q(d_ff_1_q), .preset(1'b0), .en(1'b1), .reset(CL));  // open: Qn
  assign bit_extender_8_out = {{23{comparator_1_gt}}, comparator_1_gt};  // Bit_Extender bit_extender_8
  and and_4 (IGD, d_ff_1_q, comparator_1_gt);
  assign OC = I & bit_extender_8_out;  // AND_Gate and_5, 24 bits wide
endmodule

module transf2 (
  input  [11:0] ARAI,
  input  [11:0] ARA,
  input  [7:0] DR,
  input  [7:0] DRG,
  input  [7:0] DRAI,
  input  ERG,
  input  ER,
  input  EM,
  input  strRAI,
  input  SelRAI,
  output [11:0] ARAO,
  output [7:0] DRAO,
  output strRAO,
  output SelRAO
);

  wire and_5_out, and_6_out, and_7_out, and_8_out, not_1_out, or_2_out;
  wire [7:0] and_3_out, and_4_out, bit_extender_4_out, not_3_out, or_1_out;
  wire [15:0] and_1_out, and_2_out, bit_extender_1_out, bit_extender_2_out, bit_extender_3_out, not_2_out,
       or_3_out;

  Pull_Resistor pull_resistor_1 (.node(DRG));
  assign bit_extender_1_out = {{4{1'b0}}, ARAI};  // Bit_Extender bit_extender_1
  assign bit_extender_2_out = {{4{1'b0}}, ARA};  // Bit_Extender bit_extender_2
  Pull_Resistor pull_resistor_2 (.node(DR));
  assign or_1_out = DR | DRG;  // OR_Gate or_1, 8 bits wide
  or or_2 (or_2_out, ERG, ER);
  assign bit_extender_3_out = {{15{or_2_out}}, or_2_out};  // Bit_Extender bit_extender_3
  assign bit_extender_4_out = {{7{or_2_out}}, or_2_out};  // Bit_Extender bit_extender_4
  not not_1 (not_1_out, EM);
  assign and_1_out = bit_extender_1_out & not_2_out;  // AND_Gate and_1, 16 bits wide
  assign not_2_out = ~bit_extender_3_out;  // NOT_Gate not_2, 16 bits wide
  assign and_2_out = bit_extender_3_out & bit_extender_2_out;  // AND_Gate and_2, 16 bits wide
  assign and_3_out = or_1_out & bit_extender_4_out;  // AND_Gate and_3, 8 bits wide
  assign not_3_out = ~bit_extender_4_out;  // NOT_Gate not_3, 8 bits wide
  assign and_4_out = not_3_out & DRAI;  // AND_Gate and_4, 8 bits wide
  and and_5 (and_5_out, or_2_out, not_1_out);
  and and_6 (and_6_out, strRAI, EM);
  and and_7 (and_7_out, or_2_out, not_1_out);
  and and_8 (and_8_out, SelRAI, EM);
  assign or_3_out = and_1_out | and_2_out;  // OR_Gate or_3, 16 bits wide
  Bit_Extender #(.in_width(16), .out_width(12)) bit_extender_5 (.in(or_3_out), .out(ARAO));
  assign DRAO = and_3_out | and_4_out;  // OR_Gate or_4, 8 bits wide
  or or_5 (strRAO, and_5_out, and_6_out);
  or or_6 (SelRAO, and_7_out, and_8_out);

  // Notes on the sheet:
  //   HRAO : Horloge RAm Out
  //   HRAI : Horloge RAm In
  //   DRAO : Data RAm out
  //   DRAI : Data RAm In
  //   ERAI : Enable RAm In
  //   DR : Data Rom
  //   DRG : Data Rom Game
  //   ARA : Adresse RAm
  //   ARAI : Adresse RAm In
  //   ARAO : Adresse RAm out
  //   ERAO : Enalbe RAm out
  //   strRAO : strore RAm Out
  //   strRAI : store RAm in
endmodule

module transf (
  input  H,
  input  enable,
  input  clear,
  input  [11:0] MAX,
  output [11:0] ARA,
  output [8:0] AR,
  output [11:0] ARG,
  output ERG,
  output ER,
  output EM
);

  wire and_1_out, comparator_1_eq, comparator_1_gt, comparator_2_eq, comparator_2_gt, comparator_2_lt,
       nand_1_out, or_2_out;
  wire [8:0] bit_extender_5_out, bit_extender_6_out;
  wire [11:0] bit_extender_7_out, subtractor_1_out;
  wire [15:0] adder_1_out, and_2_out, and_3_out, bit_extender_2_out, bit_extender_3_out, bit_extender_4_out,
       counter_1_q, not_1_out, or_1_out;

  Counter #(.width(16), .max('hffff)) counter_1 (
    .load(1'b0), .D({16{1'b0}}), .count(and_1_out), .Q(counter_1_q), .clk(H), .clr(clear));  // open: carry
  nand nand_1 (nand_1_out, MAX[0], MAX[1], MAX[2], MAX[3], MAX[4], MAX[5], MAX[7], MAX[8], MAX[9], MAX[10], MAX[11], MAX[6]);
  Bit_Extender #(.in_width(16), .out_width(12)) bit_extender_1 (.in(counter_1_q), .out(ARA));
  assign bit_extender_2_out = {{4{1'b0}}, MAX};  // Bit_Extender bit_extender_2
  assign bit_extender_3_out = {{15{nand_1_out}}, nand_1_out};  // Bit_Extender bit_extender_3
  Subtractor #(.width(12)) subtractor_1 (.a(ARA), .b(12'h200), .out(subtractor_1_out), .bin(1'b0));  // open: bout
  Comparator #(.width(16)) comparator_1 (
    .a(adder_1_out), .b(counter_1_q), .gt(comparator_1_gt), .eq(comparator_1_eq));  // open: lt
  and and_1 (and_1_out, comparator_1_gt, enable);
  assign bit_extender_4_out = {{4{1'b0}}, 12'h200};  // Bit_Extender bit_extender_4
  assign and_2_out = bit_extender_2_out & not_1_out;  // AND_Gate and_2, 16 bits wide
  assign not_1_out = ~bit_extender_3_out;  // NOT_Gate not_1, 16 bits wide
  assign and_3_out = bit_extender_3_out & 16'hdff;  // AND_Gate and_3, 16 bits wide
  Comparator #(.width(12)) comparator_2 (
    .a(subtractor_1_out), .b({12{1'b0}}), .gt(comparator_2_gt), .eq(comparator_2_eq), .lt(comparator_2_lt));
  assign or_1_out = and_2_out | and_3_out;  // OR_Gate or_1, 16 bits wide
  Bit_Extender #(.in_width(12), .out_width(9)) bit_extender_5 (.in(ARA), .out(bit_extender_5_out));
  and and_4 (ERG, comparator_1_gt, or_2_out);
  or or_2 (or_2_out, comparator_2_gt, comparator_2_eq);
  and and_5 (ER, comparator_2_lt, comparator_1_gt);
  Adder #(.width(16)) adder_1 (.a(bit_extender_4_out), .b(or_1_out), .out(adder_1_out), .cin(1'b0));  // open: cout
  assign bit_extender_6_out = {{8{ER}}, ER};  // Bit_Extender bit_extender_6
  assign bit_extender_7_out = {{11{ERG}}, ERG};  // Bit_Extender bit_extender_7
  D_Flip_Flop d_ff_1 (.clk(H), .D(comparator_1_eq), .Q(EM), .preset(1'b0), .en(enable), .reset(clear));  // open: Qn
  assign AR = bit_extender_5_out & bit_extender_6_out;  // AND_Gate and_6, 9 bits wide
  assign ARG = subtractor_1_out & bit_extender_7_out;  // AND_Gate and_7, 12 bits wide

  // Notes on the sheet:
  //   ARA : Adresse RAm
  //   AR : Adresse Rom
  //   ARG : Adresse Rom Game
  //   ERG : Enable Rom Game
  //   ER : Enable Rom
  //   EM : Enable Microprocesseur
  //   H : Horloge
endmodule

module VALUEM (
  input  [7:0] Input,
  input  [7:0] Max,
  output [7:0] Output
);

  wire comparator_1_gt;
  wire [7:0] and_1_out, and_2_out, and_3_out, bit_extender_1_out, maskmax_1_output, not_1_out;

  // Probe on Input
  // Probe on Max
  Comparator #(.mode("unsigned")) comparator_1 (.a(Input), .b(Max), .gt(comparator_1_gt));  // open: eq, lt
  assign bit_extender_1_out = {{7{comparator_1_gt}}, comparator_1_gt};  // Bit_Extender bit_extender_1
  MASKMAX maskmax_1 (.Max(Max), .Output(maskmax_1_output));
  assign and_1_out = Input & maskmax_1_output;  // AND_Gate and_1, 8 bits wide
  // Probe on maskmax_1_output
  assign not_1_out = ~bit_extender_1_out;  // NOT_Gate not_1, 8 bits wide
  assign and_2_out = not_1_out & Input;  // AND_Gate and_2, 8 bits wide
  assign and_3_out = bit_extender_1_out & and_1_out;  // AND_Gate and_3, 8 bits wide
  // Probe on Output
  assign Output = and_2_out | and_3_out;  // OR_Gate or_1, 8 bits wide

  // Notes on the sheet:
  //   if (Input <= Max) =>>> Input
  //   if(Input > Max)
endmodule

module MASKMAX (
  input  [7:0] Max,
  output [7:0] Output
);

  wire cod8_1_validate, not_1_out, or_1_out;
  wire [2:0] cod8_1_output;
  wire [7:0] and_1_out, and_2_out, bit_extender_1_out, bit_extender_2_out, decoder_1_out0, subtractor_1_out;

  // Probe on Max
  COD8 cod8_1 (
    .Enable(1'b1), .Validate(cod8_1_validate), .Output(cod8_1_output), .Input_0(Max[0]), .Input_1(Max[1]),
    .Input_2(Max[2]), .Input_3(Max[3]), .Input_4(Max[4]), .Input_5(Max[5]), .Input_6(Max[6]), .Input_7(Max[7]));  // open: Error
  Decoder #(.select(3), .disabled(0)) decoder_1 (
    .out0(decoder_1_out0[0]), .out1(decoder_1_out0[1]), .out2(decoder_1_out0[2]), .out3(decoder_1_out0[3]),
    .out4(decoder_1_out0[4]), .out5(decoder_1_out0[5]), .out6(decoder_1_out0[6]), .out7(decoder_1_out0[7]),
    .sel(cod8_1_output), .en(cod8_1_validate));
  Subtractor subtractor_1 (.a(decoder_1_out0), .b(8'h1), .out(subtractor_1_out), .bin(1'b0));  // open: bout
  // Probe on subtractor_1_out
  // Probe on subtractor_1_out
  or or_1 (or_1_out, subtractor_1_out[0], subtractor_1_out[1], subtractor_1_out[2], subtractor_1_out[3], subtractor_1_out[4], subtractor_1_out[5], subtractor_1_out[6], subtractor_1_out[7]);
  not not_1 (not_1_out, or_1_out);
  assign bit_extender_1_out = {{7{not_1_out}}, not_1_out};  // Bit_Extender bit_extender_1
  assign bit_extender_2_out = {{7{or_1_out}}, or_1_out};  // Bit_Extender bit_extender_2
  assign and_1_out = 8'h1 & bit_extender_1_out;  // AND_Gate and_1, 8 bits wide
  assign and_2_out = bit_extender_2_out & subtractor_1_out;  // AND_Gate and_2, 8 bits wide
  // Probe on Output
  assign Output = and_1_out | and_2_out;  // OR_Gate or_2, 8 bits wide
  // Probe on Output

  // Notes on the sheet:
  //   Mask creation
  //   Mask != 0
endmodule
