// Logisim project mini_chip8.circ as structural Verilog: 8 circuits, main circuit main
module main (
  output out_1,
  output C8PIC,
  output BC_test,
  output MAZE,
  output BCD,
  output X_MIRROR,
  output PONG,
  output BREAKOUT,
  output VOITURE
);

  wire _0_out, _1_out, _2_out, _3_out, _4_out, _5_out, _6_out, _7_out, _8_out, _9_out, A_out, B_out,
       button_1_out, C_out, chip8_1_ledm, chip8_1_son, D_out, E_out, F_out, games_1_p3, hpbeep_1_out_3,
       hpbeep_1_out_4, MA_out, RESET_out;
  wire [3:0] chip8_1_r;
  wire [4:0] chip8_1_scy, codh_1_output;
  wire [5:0] chip8_1_scx;
  wire [7:0] games_1_p4;
  wire [11:0] games_1_p2, games_1_p5;
  wire [31:0] lc64_1_out_7, lc64_1_out_8, lc64_1_out_9, lc64_1_out_10, lc64_1_out_11, lc64_1_out_12,
       lc64_1_out_13, lc64_1_out_14, lc64_1_out_15, lc64_1_out_16, lc64_1_out_17, lc64_1_out_18,
       lc64_1_out_19, lc64_1_out_20, lc64_1_out_21, lc64_1_out_22, lc64_1_out_23, lc64_1_out_24,
       lc64_1_out_25, lc64_1_out_26, lc64_1_out_27, lc64_1_out_28, lc64_1_out_29, lc64_1_out_30,
       lc64_1_out_31, lc64_1_out_32, lc64_1_out_33, lc64_1_out_34, lc64_1_out_35, lc64_1_out_36,
       lc64_1_out_37, lc64_1_out_38, lc64_1_out_39, lc64_1_out_40, lc64_1_out_41, lc64_1_out_42,
       lc64_1_out_43, lc64_1_out_44, lc64_1_out_45, lc64_1_out_46, lc64_1_out_47, lc64_1_out_48,
       lc64_1_out_49, lc64_1_out_50, lc64_1_out_51, lc64_1_out_52, lc64_1_out_53, lc64_1_out_54,
       lc64_1_out_55, lc64_1_out_56, lc64_1_out_57, lc64_1_out_58, lc64_1_out_59, lc64_1_out_60,
       lc64_1_out_61, lc64_1_out_62, lc64_1_out_63, lc64_1_out_64, lc64_1_out_65, lc64_1_out_66,
       lc64_1_out_67, lc64_1_out_68, lc64_1_out_69, lc64_1_out_70;

  LED led_1 (.in(chip8_1_ledm));
  Button MA (.out(MA_out));
  Button RESET (.out(RESET_out));
  Button button_1 (.out(button_1_out));
  // GAMES games_1: pin names not known; wires that end beside it: button_1_out, games_1_p2, games_1_p3, games_1_p4, games_1_p5, {VOITURE, BREAKOUT, PONG, X_MIRROR, BCD, MAZE, BC_test, C8PIC}
  CHIP8 chip8_1 (
    .MA(MA_out), .RESET(RESET_out), .CL(codh_1_output), .SCX(chip8_1_scx), .SCY(chip8_1_scy),
    .SCS(chip8_1_r[1]), .SSCP(chip8_1_r[2]), .GA(games_1_p2), .H(chip8_1_r[3]), .R(chip8_1_r[0]),
    .GD(games_1_p4), .Gsel(games_1_p3), .SON(chip8_1_son), .LedM(chip8_1_ledm), .in_4(games_1_p5));
  DotMatrix #(.matrixcols(32), .matrixrows(32)) dotmatrix_1 (
    .col0(lc64_1_out_7), .col1(lc64_1_out_8), .col2(lc64_1_out_9), .col3(lc64_1_out_10),
    .col4(lc64_1_out_11), .col5(lc64_1_out_12), .col6(lc64_1_out_13), .col7(lc64_1_out_14),
    .col8(lc64_1_out_15), .col9(lc64_1_out_16), .col10(lc64_1_out_17), .col11(lc64_1_out_18),
    .col12(lc64_1_out_19), .col13(lc64_1_out_20), .col14(lc64_1_out_21), .col15(lc64_1_out_22),
    .col16(lc64_1_out_23), .col17(lc64_1_out_24), .col18(lc64_1_out_25), .col19(lc64_1_out_26),
    .col20(lc64_1_out_27), .col21(lc64_1_out_28), .col22(lc64_1_out_29), .col23(lc64_1_out_30),
    .col24(lc64_1_out_31), .col25(lc64_1_out_32), .col26(lc64_1_out_33), .col27(lc64_1_out_34),
    .col28(lc64_1_out_35), .col29(lc64_1_out_36), .col30(lc64_1_out_37), .col31(lc64_1_out_38));
  LC64 lc64_1 (
    .E(chip8_1_r[2]), .X(chip8_1_scx), .Y(chip8_1_scy), .H(chip8_1_r[3]), .I(chip8_1_r[1]), .C(chip8_1_r[0]),
    .out_7(lc64_1_out_7), .out_8(lc64_1_out_8), .out_9(lc64_1_out_9), .out_10(lc64_1_out_10),
    .out_11(lc64_1_out_11), .out_12(lc64_1_out_12), .out_13(lc64_1_out_13), .out_14(lc64_1_out_14),
    .out_15(lc64_1_out_15), .out_16(lc64_1_out_16), .out_17(lc64_1_out_17), .out_18(lc64_1_out_18),
    .out_19(lc64_1_out_19), .out_20(lc64_1_out_20), .out_21(lc64_1_out_21), .out_22(lc64_1_out_22),
    .out_23(lc64_1_out_23), .out_24(lc64_1_out_24), .out_25(lc64_1_out_25), .out_26(lc64_1_out_26),
    .out_27(lc64_1_out_27), .out_28(lc64_1_out_28), .out_29(lc64_1_out_29), .out_30(lc64_1_out_30),
    .out_31(lc64_1_out_31), .out_32(lc64_1_out_32), .out_33(lc64_1_out_33), .out_34(lc64_1_out_34),
    .out_35(lc64_1_out_35), .out_36(lc64_1_out_36), .out_37(lc64_1_out_37), .out_38(lc64_1_out_38),
    .out_39(lc64_1_out_39), .out_40(lc64_1_out_40), .out_41(lc64_1_out_41), .out_42(lc64_1_out_42),
    .out_43(lc64_1_out_43), .out_44(lc64_1_out_44), .out_45(lc64_1_out_45), .out_46(lc64_1_out_46),
    .out_47(lc64_1_out_47), .out_48(lc64_1_out_48), .out_49(lc64_1_out_49), .out_50(lc64_1_out_50),
    .out_51(lc64_1_out_51), .out_52(lc64_1_out_52), .out_53(lc64_1_out_53), .out_54(lc64_1_out_54),
    .out_55(lc64_1_out_55), .out_56(lc64_1_out_56), .out_57(lc64_1_out_57), .out_58(lc64_1_out_58),
    .out_59(lc64_1_out_59), .out_60(lc64_1_out_60), .out_61(lc64_1_out_61), .out_62(lc64_1_out_62),
    .out_63(lc64_1_out_63), .out_64(lc64_1_out_64), .out_65(lc64_1_out_65), .out_66(lc64_1_out_66),
    .out_67(lc64_1_out_67), .out_68(lc64_1_out_68), .out_69(lc64_1_out_69), .out_70(lc64_1_out_70));
  Button _2 (.out(_2_out));
  Button _1 (.out(_1_out));
  Button _4 (.out(_4_out));
  Button _5 (.out(_5_out));
  Button _8 (.out(_8_out));
  Button _7 (.out(_7_out));
  Button A (.out(A_out));
  Button _0 (.out(_0_out));
  Button _3 (.out(_3_out));
  Button _6 (.out(_6_out));
  Button _9 (.out(_9_out));
  Button B (.out(B_out));
  Button C (.out(C_out));
  Button D (.out(D_out));
  Button E (.out(E_out));
  Button F (.out(F_out));
  DotMatrix #(.matrixcols(32), .matrixrows(32)) dotmatrix_2 (
    .col0(lc64_1_out_39), .col1(lc64_1_out_40), .col2(lc64_1_out_41), .col3(lc64_1_out_42),
    .col4(lc64_1_out_43), .col5(lc64_1_out_44), .col6(lc64_1_out_45), .col7(lc64_1_out_46),
    .col8(lc64_1_out_47), .col9(lc64_1_out_48), .col10(lc64_1_out_49), .col11(lc64_1_out_50),
    .col12(lc64_1_out_51), .col13(lc64_1_out_52), .col14(lc64_1_out_53), .col15(lc64_1_out_54),
    .col16(lc64_1_out_55), .col17(lc64_1_out_56), .col18(lc64_1_out_57), .col19(lc64_1_out_58),
    .col20(lc64_1_out_59), .col21(lc64_1_out_60), .col22(lc64_1_out_61), .col23(lc64_1_out_62),
    .col24(lc64_1_out_63), .col25(lc64_1_out_64), .col26(lc64_1_out_65), .col27(lc64_1_out_66),
    .col28(lc64_1_out_67), .col29(lc64_1_out_68), .col30(lc64_1_out_69), .col31(lc64_1_out_70));
  CODH codh_1 (
    .Enable(1'b1), .Validate(codh_1_output[4]), .Output(codh_1_output[3:0]), .Input_0(_0_out),
    .Input_1(_1_out), .Input_2(_2_out), .Input_3(_3_out), .Input_4(_4_out), .Input_5(_5_out),
    .Input_6(_6_out), .Input_7(_7_out), .Input_8(_8_out), .Input_9(_9_out), .Input_10(A_out),
    .Input_11(B_out), .Input_12(C_out), .Input_13(D_out), .Input_14(E_out), .Input_15(F_out));  // open: Error
  HPBEEP hpbeep_1 (.in_1(chip8_1_son), .out_2(out_1), .out_3(hpbeep_1_out_3), .out_4(hpbeep_1_out_4));

  // Notes on the sheet:
  //   GAMES
endmodule

module main2 (
  output out_1,
  output out_2,
  output C8PIC,
  output BC_test,
  output MAZE,
  output BCD,
  output X_MIRROR,
  output PONG,
  output BREAKOUT,
  output VOITURE
);

  wire _0_out, _1_out, _2_out, _3_out, _4_out, _5_out, _6_out, _7_out, _8_out, _9_out, A_out, B_out,
       button_1_out, C_out, chip8_1_son, D_out, E_out, F_out, games_1_p3, hpbeep_1_out_3, hpbeep_1_out_4,
       keyboard02_1_out_6, MA_out, RESET_out;
  wire [3:0] chip8_1_r, keyboard01_1_out_5, keyboard01_2_out_5, keyboard01_3_out_5, keyboard01_4_out_5;
  wire [4:0] chip8_1_scy, keyboard02_1_out_5;
  wire [5:0] chip8_1_scx;
  wire [7:0] games_1_p4;
  wire [11:0] games_1_p2, games_1_p5;
  wire [31:0] lc64_1_out_7, lc64_1_out_8, lc64_1_out_9, lc64_1_out_10, lc64_1_out_11, lc64_1_out_12,
       lc64_1_out_13, lc64_1_out_14, lc64_1_out_15, lc64_1_out_16, lc64_1_out_17, lc64_1_out_18,
       lc64_1_out_19, lc64_1_out_20, lc64_1_out_21, lc64_1_out_22, lc64_1_out_23, lc64_1_out_24,
       lc64_1_out_25, lc64_1_out_26, lc64_1_out_27, lc64_1_out_28, lc64_1_out_29, lc64_1_out_30,
       lc64_1_out_31, lc64_1_out_32, lc64_1_out_33, lc64_1_out_34, lc64_1_out_35, lc64_1_out_36,
       lc64_1_out_37, lc64_1_out_38, lc64_1_out_39, lc64_1_out_40, lc64_1_out_41, lc64_1_out_42,
       lc64_1_out_43, lc64_1_out_44, lc64_1_out_45, lc64_1_out_46, lc64_1_out_47, lc64_1_out_48,
       lc64_1_out_49, lc64_1_out_50, lc64_1_out_51, lc64_1_out_52, lc64_1_out_53, lc64_1_out_54,
       lc64_1_out_55, lc64_1_out_56, lc64_1_out_57, lc64_1_out_58, lc64_1_out_59, lc64_1_out_60,
       lc64_1_out_61, lc64_1_out_62, lc64_1_out_63, lc64_1_out_64, lc64_1_out_65, lc64_1_out_66,
       lc64_1_out_67, lc64_1_out_68, lc64_1_out_69, lc64_1_out_70;

  Button MA (.out(MA_out));
  Button RESET (.out(RESET_out));
  Button button_1 (.out(button_1_out));
  // GAMES games_1: pin names not known; wires that end beside it: button_1_out, games_1_p2, games_1_p3, games_1_p4, games_1_p5, {VOITURE, BREAKOUT, PONG, X_MIRROR, BCD, MAZE, BC_test, C8PIC}
  CHIP8 chip8_1 (
    .MA(MA_out), .RESET(RESET_out), .CL(keyboard02_1_out_5), .SCX(chip8_1_scx), .SCY(chip8_1_scy),
    .SCS(chip8_1_r[1]), .SSCP(chip8_1_r[2]), .GA(games_1_p2), .H(chip8_1_r[3]), .R(chip8_1_r[0]),
    .GD(games_1_p4), .Gsel(games_1_p3), .SON(chip8_1_son), .LedM(out_1), .in_4(games_1_p5));
  DotMatrix #(.matrixcols(32), .matrixrows(32)) dotmatrix_1 (
    .col0(lc64_1_out_7), .col1(lc64_1_out_8), .col2(lc64_1_out_9), .col3(lc64_1_out_10),
    .col4(lc64_1_out_11), .col5(lc64_1_out_12), .col6(lc64_1_out_13), .col7(lc64_1_out_14),
    .col8(lc64_1_out_15), .col9(lc64_1_out_16), .col10(lc64_1_out_17), .col11(lc64_1_out_18),
    .col12(lc64_1_out_19), .col13(lc64_1_out_20), .col14(lc64_1_out_21), .col15(lc64_1_out_22),
    .col16(lc64_1_out_23), .col17(lc64_1_out_24), .col18(lc64_1_out_25), .col19(lc64_1_out_26),
    .col20(lc64_1_out_27), .col21(lc64_1_out_28), .col22(lc64_1_out_29), .col23(lc64_1_out_30),
    .col24(lc64_1_out_31), .col25(lc64_1_out_32), .col26(lc64_1_out_33), .col27(lc64_1_out_34),
    .col28(lc64_1_out_35), .col29(lc64_1_out_36), .col30(lc64_1_out_37), .col31(lc64_1_out_38));
  LC64 lc64_1 (
    .E(chip8_1_r[2]), .X(chip8_1_scx), .Y(chip8_1_scy), .H(chip8_1_r[3]), .I(chip8_1_r[1]), .C(chip8_1_r[0]),
    .out_7(lc64_1_out_7), .out_8(lc64_1_out_8), .out_9(lc64_1_out_9), .out_10(lc64_1_out_10),
    .out_11(lc64_1_out_11), .out_12(lc64_1_out_12), .out_13(lc64_1_out_13), .out_14(lc64_1_out_14),
    .out_15(lc64_1_out_15), .out_16(lc64_1_out_16), .out_17(lc64_1_out_17), .out_18(lc64_1_out_18),
    .out_19(lc64_1_out_19), .out_20(lc64_1_out_20), .out_21(lc64_1_out_21), .out_22(lc64_1_out_22),
    .out_23(lc64_1_out_23), .out_24(lc64_1_out_24), .out_25(lc64_1_out_25), .out_26(lc64_1_out_26),
    .out_27(lc64_1_out_27), .out_28(lc64_1_out_28), .out_29(lc64_1_out_29), .out_30(lc64_1_out_30),
    .out_31(lc64_1_out_31), .out_32(lc64_1_out_32), .out_33(lc64_1_out_33), .out_34(lc64_1_out_34),
    .out_35(lc64_1_out_35), .out_36(lc64_1_out_36), .out_37(lc64_1_out_37), .out_38(lc64_1_out_38),
    .out_39(lc64_1_out_39), .out_40(lc64_1_out_40), .out_41(lc64_1_out_41), .out_42(lc64_1_out_42),
    .out_43(lc64_1_out_43), .out_44(lc64_1_out_44), .out_45(lc64_1_out_45), .out_46(lc64_1_out_46),
    .out_47(lc64_1_out_47), .out_48(lc64_1_out_48), .out_49(lc64_1_out_49), .out_50(lc64_1_out_50),
    .out_51(lc64_1_out_51), .out_52(lc64_1_out_52), .out_53(lc64_1_out_53), .out_54(lc64_1_out_54),
    .out_55(lc64_1_out_55), .out_56(lc64_1_out_56), .out_57(lc64_1_out_57), .out_58(lc64_1_out_58),
    .out_59(lc64_1_out_59), .out_60(lc64_1_out_60), .out_61(lc64_1_out_61), .out_62(lc64_1_out_62),
    .out_63(lc64_1_out_63), .out_64(lc64_1_out_64), .out_65(lc64_1_out_65), .out_66(lc64_1_out_66),
    .out_67(lc64_1_out_67), .out_68(lc64_1_out_68), .out_69(lc64_1_out_69), .out_70(lc64_1_out_70));
  Button _1 (.out(_1_out));
  Button _4 (.out(_4_out));
  Button _7 (.out(_7_out));
  Button A (.out(A_out));
  Button _3 (.out(_3_out));
  Button _2 (.out(_2_out));
  Button _6 (.out(_6_out));
  Button _5 (.out(_5_out));
  Button _9 (.out(_9_out));
  Button _8 (.out(_8_out));
  Button _0 (.out(_0_out));
  Button B (.out(B_out));
  keyboard01 keyboard01_1 (.in_1(_1_out), .in_2(_2_out), .in_3(_3_out), .in_4(C_out), .out_5(keyboard01_1_out_5));
  Button C (.out(C_out));
  Button D (.out(D_out));
  keyboard01 keyboard01_2 (.in_1(_4_out), .in_2(_5_out), .in_3(_6_out), .in_4(D_out), .out_5(keyboard01_2_out_5));
  keyboard02 keyboard02_1 (
    .in_1(keyboard01_1_out_5), .in_2(keyboard01_2_out_5), .in_3(keyboard01_3_out_5),
    .in_4(keyboard01_4_out_5), .out_5(keyboard02_1_out_5), .out_6(keyboard02_1_out_6));
  LED led_1 (.in(keyboard02_1_out_6));
  keyboard01 keyboard01_3 (.in_1(_7_out), .in_2(_8_out), .in_3(_9_out), .in_4(E_out), .out_5(keyboard01_3_out_5));
  Button E (.out(E_out));
  Button F (.out(F_out));
  keyboard01 keyboard01_4 (.in_1(A_out), .in_2(_0_out), .in_3(B_out), .in_4(F_out), .out_5(keyboard01_4_out_5));
  DotMatrix #(.matrixcols(32), .matrixrows(32)) dotmatrix_2 (
    .col0(lc64_1_out_39), .col1(lc64_1_out_40), .col2(lc64_1_out_41), .col3(lc64_1_out_42),
    .col4(lc64_1_out_43), .col5(lc64_1_out_44), .col6(lc64_1_out_45), .col7(lc64_1_out_46),
    .col8(lc64_1_out_47), .col9(lc64_1_out_48), .col10(lc64_1_out_49), .col11(lc64_1_out_50),
    .col12(lc64_1_out_51), .col13(lc64_1_out_52), .col14(lc64_1_out_53), .col15(lc64_1_out_54),
    .col16(lc64_1_out_55), .col17(lc64_1_out_56), .col18(lc64_1_out_57), .col19(lc64_1_out_58),
    .col20(lc64_1_out_59), .col21(lc64_1_out_60), .col22(lc64_1_out_61), .col23(lc64_1_out_62),
    .col24(lc64_1_out_63), .col25(lc64_1_out_64), .col26(lc64_1_out_65), .col27(lc64_1_out_66),
    .col28(lc64_1_out_67), .col29(lc64_1_out_68), .col30(lc64_1_out_69), .col31(lc64_1_out_70));
  HPBEEP hpbeep_1 (.in_1(chip8_1_son), .out_2(out_2), .out_3(hpbeep_1_out_3), .out_4(hpbeep_1_out_4));

  // Notes on the sheet:
  //   GAMES
endmodule

module CPU (
  input  [7:0] DR,
  input  enable,
  input  [4:0] CL,
  input  SCP,
  input  H,
  input  clear,
  output SON,
  output [11:0] AR,
  output [7:0] DR_2,
  output SR,
  output RE,
  output [5:0] SCX,
  output [4:0] SCY,
  output SCstore,
  output SSCP
);

  wire alu_1_ec, alu_1_scmpgame, alu_1_scmpson, alu_1_si, alu_1_snbrsaut, alu_1_spc, alu_1_ssaut, alu_1_svf,
       alu_1_svx, and_1_out, cpm_1_end, cpm_1_t1, cpm_1_t2, d_ff_1_q, d_ff_1_qn, dec_1__00e0, dec_1__00ee,
       dec_1__0nnn, dec_1__1nnn, dec_1__2nnn, dec_1__3xkk, dec_1__4xkk, dec_1__5xy0, dec_1__6xkk,
       dec_1__7xkk, dec_1__8x0e, dec_1__8x06, dec_1__8xy0, dec_1__8xy1, dec_1__8xy2, dec_1__8xy3,
       dec_1__8xy4, dec_1__8xy5, dec_1__8xy7, dec_1__9xy0, dec_1_annn, dec_1_bnnn, dec_1_cxkk, dec_1_dxyk,
       dec_1_ex9e, dec_1_exa1, dec_1_fx0a, dec_1_fx1e, dec_1_fx07, dec_1_fx15, dec_1_fx18, dec_1_fx29,
       dec_1_fx33, dec_1_fx55, dec_1_fx65, loadr_1_end, loadr_1_spc, not_1_out, or_1_out, or_2_out, or_3_out,
       or_5_out;
  wire [3:0] alu_1_ax, alu_1_ay, alu_1_nbrsaut_2, alu_1_nc, dec_1_ax, dec_1_ay, dec_1_k, nbrsaut_q;
  wire [7:0] alu_1_cmpgame_2, alu_1_vf, alu_1_vx_2, compteurJeu_q, dec_1_kk, regi16_1_p12, regi16_1_p13,
       regi16_1_p14;
  wire [11:0] alu_1_ar, alu_1_i_2, alu_1_pc_2, alu_1_saut_2, and_2_out, and_3_out, bit_extender_1_out,
       dec_1_nnn, I_adresse_memoire_q, loadr_1_pc_2, not_2_out, or_4_out, PC_q, ram_1_data;
  wire [15:0] alu_1_cmpson_2, compteurSon_q, loadr_1_opcode;

  and and_1 (and_1_out, enable, d_ff_1_qn);
  or or_1 (or_1_out, cpm_1_end, or_2_out);
  not not_1 (not_1_out, enable);
  loadR loadr_1 (
    .DR(DR), .enable(and_1_out), .H(H), .clear(or_1_out), .PC(PC_q), .opcode(loadr_1_opcode),
    .\end (loadr_1_end), .SPC(loadr_1_spc), .PC_2(loadr_1_pc_2));
  or or_2 (or_2_out, not_1_out, clear);
  DEC dec_1 (
    .enable(loadr_1_end), .opcode(loadr_1_opcode), .AX(dec_1_ax), .AY(dec_1_ay), .K(dec_1_k), .KK(dec_1_kk),
    .NNN(dec_1_nnn), ._00E0(dec_1__00e0), ._00EE(dec_1__00ee), ._0NNN(dec_1__0nnn), ._1NNN(dec_1__1nnn),
    ._2NNN(dec_1__2nnn), .ANNN(dec_1_annn), .BNNN(dec_1_bnnn), ._3XKK(dec_1__3xkk), ._4XKK(dec_1__4xkk),
    ._6XKK(dec_1__6xkk), ._7XKK(dec_1__7xkk), .CXKK(dec_1_cxkk), ._5XY0(dec_1__5xy0), ._8XY0(dec_1__8xy0),
    ._8XY1(dec_1__8xy1), ._8XY2(dec_1__8xy2), ._8XY3(dec_1__8xy3), ._8XY4(dec_1__8xy4), ._8XY5(dec_1__8xy5),
    ._8XY7(dec_1__8xy7), ._9XY0(dec_1__9xy0), .DXYK(dec_1_dxyk), ._8X06(dec_1__8x06), ._8X0E(dec_1__8x0e),
    .EX9E(dec_1_ex9e), .EXA1(dec_1_exa1), .FX07(dec_1_fx07), .FX0A(dec_1_fx0a), .FX15(dec_1_fx15),
    .FX18(dec_1_fx18), .FX1E(dec_1_fx1e), .FX29(dec_1_fx29), .FX33(dec_1_fx33), .FX55(dec_1_fx55),
    .FX65(dec_1_fx65));
  ALU alu_1 (
    .X(dec_1_ax), .Y(dec_1_ay), .VX(regi16_1_p13), .VY(regi16_1_p14), .saut(ram_1_data), .NNN(dec_1_nnn),
    .PC(PC_q), .nbrsaut(nbrsaut_q), .KK(dec_1_kk), ._0NNN(dec_1__0nnn), ._00E0(dec_1__00e0),
    ._00EE(dec_1__00ee), ._1NNN(dec_1__1nnn), ._2NNN(dec_1__2nnn), ._3XKK(dec_1__3xkk), ._4XKK(dec_1__4xkk),
    ._5XY0(dec_1__5xy0), ._6XKK(dec_1__6xkk), ._7XKK(dec_1__7xkk), ._8X06(dec_1__8x06), ._8X0E(dec_1__8x0e),
    ._8XY0(dec_1__8xy0), ._8XY1(dec_1__8xy1), ._8XY2(dec_1__8xy2), ._8XY3(dec_1__8xy3), ._8XY4(dec_1__8xy4),
    ._8XY5(dec_1__8xy5), ._8XY7(dec_1__8xy7), ._9XY0(dec_1__9xy0), .ANNN(dec_1_annn), .BNNN(dec_1_bnnn),
    .CXKK(dec_1_cxkk), .DXYK(dec_1_dxyk), .EX9E(dec_1_ex9e), .EXA1(dec_1_exa1), .FX07(dec_1_fx07),
    .FX0A(dec_1_fx0a), .FX15(dec_1_fx15), .FX18(dec_1_fx18), .FX1E(dec_1_fx1e), .FX29(dec_1_fx29),
    .FX33(dec_1_fx33), .FX55(dec_1_fx55), .FX65(dec_1_fx65), .SCP(SCP), .K(dec_1_k), .CMPGAME(compteurJeu_q),
    .V0(regi16_1_p12), .CL(CL), .I(I_adresse_memoire_q), .DR(DR), .H(H), .T1(cpm_1_t1), .T2(cpm_1_t2),
    .RE(RE), .Snbrsaut(alu_1_snbrsaut), .nbrsaut_2(alu_1_nbrsaut_2), .saut_2(alu_1_saut_2),
    .Ssaut(alu_1_ssaut), .VF(alu_1_vf), .SVF(alu_1_svf), .AY(alu_1_ay), .PC_2(alu_1_pc_2), .SPC(alu_1_spc),
    .I_2(alu_1_i_2), .SI(alu_1_si), .AR(alu_1_ar), .SCX(SCX), .SCY(SCY), .SCstore(SCstore), .SSCP(SSCP),
    .CMPGAME_2(alu_1_cmpgame_2), .SCMPGAME(alu_1_scmpgame), .CMPSON_2(alu_1_cmpson_2),
    .SCMPSON(alu_1_scmpson), .DR_2(DR_2), .SR(SR), .VX_2(alu_1_vx_2), .SVX(alu_1_svx), .AX(alu_1_ax),
    .EC(alu_1_ec), .NC(alu_1_nc), .SON(SON), .CMPSON(compteurSon_q));
  CPM cpm_1 (
    .enable(d_ff_1_q), .H(H), .NC(alu_1_nc), .EC(alu_1_ec), .T1(cpm_1_t1), .T2(cpm_1_t2), .\end (cpm_1_end));  // open: T0, T3, T4, T5, T6, T7
  D_Flip_Flop d_ff_1 (
    .clk(loadr_1_end), .D(1'b1), .Q(d_ff_1_q), .Qn(d_ff_1_qn), .preset(1'b0), .en(1'b1), .reset(or_3_out));
  or or_3 (or_3_out, or_2_out, cpm_1_end);
  assign or_4_out = loadr_1_pc_2 | alu_1_pc_2;  // OR_Gate or_4, 12 bits wide
  or or_5 (or_5_out, loadr_1_spc, alu_1_spc);
  Register #(.width(12)) PC (.D(or_4_out), .en(or_5_out), .Q(PC_q), .clk(H), .clr(or_2_out));
  Register compteurJeu (.D(alu_1_cmpgame_2), .en(alu_1_scmpgame), .Q(compteurJeu_q), .clk(H), .clr(or_2_out));
  Register #(.width(12)) I_adresse_memoire (
    .D(alu_1_i_2), .en(alu_1_si), .Q(I_adresse_memoire_q), .clk(H), .clr(or_2_out));
  // REGI16 regi16_1: pin names not known; wires that end beside it: alu_1_vx_2, alu_1_ax, alu_1_svx, 1'b1, alu_1_ay, 1'b1, H, 1'b1, or_2_out, alu_1_vf, alu_1_svf, regi16_1_p12, regi16_1_p13, regi16_1_p14
  assign bit_extender_1_out = {{11{d_ff_1_qn}}, d_ff_1_qn};  // Bit_Extender bit_extender_1
  Register #(.width(16)) compteurSon (
    .D(alu_1_cmpson_2), .en(alu_1_scmpson), .Q(compteurSon_q), .clk(H), .clr(or_2_out));
  Register #(.width(4)) nbrsaut (.D(alu_1_nbrsaut_2), .en(alu_1_snbrsaut), .Q(nbrsaut_q), .clk(H), .clr(or_2_out));
  RAM #(.addrWidth(4), .dataWidth(12), .bus("separate")) ram_1 (
    .addr(nbrsaut_q), .din(alu_1_saut_2), .data(ram_1_data), .str(alu_1_ssaut), .sel(1'b1), .clk(H),
    .ld(1'b1), .clr(or_2_out));
  assign not_2_out = ~bit_extender_1_out;  // NOT_Gate not_2, 12 bits wide
  assign and_2_out = bit_extender_1_out & PC_q;  // AND_Gate and_2, 12 bits wide
  assign and_3_out = alu_1_ar & not_2_out;  // AND_Gate and_3, 12 bits wide
  assign AR = and_2_out | and_3_out;  // OR_Gate or_6, 12 bits wide

  // Notes on the sheet:
  //   saut
endmodule

module CHIP8 (
  input  MA,
  input  RESET,
  input  [4:0] CL,
  input  [11:0] in_4,
  input  [7:0] GD,
  output LedM,
  output SON,
  output R,
  output SCS,
  output SSCP,
  output H,
  output [5:0] SCX,
  output [4:0] SCY,
  output Gsel,
  output [11:0] GA
);

  wire and_1_out, clock_1_out, cpu_1_re, cpu_1_scstore, cpu_1_sr, cpu_1_sscp, graf_1_do, graf_1_endi,
       ma_1_ma_2, ma_1_r, trfc_1_clearra, trfc_1_em, trfc_1_er, trfc_1_hra, trfc_1_selrao, trfc_1_strrao;
  wire [4:0] cpu_1_scy;
  wire [5:0] cpu_1_scx;
  wire [7:0] cpu_1_dr_2, ram_1_data, rom_1_data, trfc_1_drao;
  wire [8:0] trfc_1_ar;
  wire [11:0] cpu_1_ar, trfc_1_arao;

  MA ma_1 (.MA(MA), .RESET(RESET), .LedM(LedM), .MA_2(ma_1_ma_2), .R(ma_1_r));
  Clock clock_1 (.out(clock_1_out));
  TRFC trfc_1 (
    .enable(ma_1_ma_2), .clear(ma_1_r), .DRAI(cpu_1_dr_2), .ARAI(cpu_1_ar), .strRAI(cpu_1_sr), .selRAI(1'b1),
    .AR(trfc_1_ar), .ER(trfc_1_er), .ARAO(trfc_1_arao), .DRAO(trfc_1_drao), .strRAO(trfc_1_strrao),
    .SelRAO(trfc_1_selrao), .HRA(trfc_1_hra), .clearRA(trfc_1_clearra), .ARG(GA), .ERG(Gsel), .DRG(GD),
    .DR(rom_1_data), .H(clock_1_out), .EM(trfc_1_em), .MAX(in_4));
  ROM #(.addrWidth(9)) rom_1 (.addr(trfc_1_ar), .data(rom_1_data), .sel(trfc_1_er));
  RAM #(.addrWidth(12), .bus("separate")) ram_1 (
    .addr(trfc_1_arao), .din(trfc_1_drao), .data(ram_1_data), .str(trfc_1_strrao), .sel(trfc_1_selrao),
    .clk(trfc_1_hra), .ld(1'b1), .clr(trfc_1_clearra));
  and and_1 (and_1_out, graf_1_endi, trfc_1_em);
  CPU cpu_1 (
    .DR(ram_1_data), .enable(and_1_out), .CL(CL), .SCP(graf_1_do), .H(clock_1_out), .clear(ma_1_r),
    .AR(cpu_1_ar), .DR_2(cpu_1_dr_2), .SR(cpu_1_sr), .RE(cpu_1_re), .SCX(cpu_1_scx), .SCY(cpu_1_scy),
    .SCstore(cpu_1_scstore), .SSCP(cpu_1_sscp), .SON(SON));
  GRAF graf_1 (
    .DO(graf_1_do), .AL(cpu_1_scx), .AL_2(SCX), .AC(cpu_1_scy), .AC_2(SCY), .E(ma_1_ma_2), .M(and_1_out),
    .clear(R), .R(ma_1_r), .Enable(SSCP), .D(cpu_1_sscp), .DIS(SCS), .H_2(H), .H(clock_1_out),
    .Store(cpu_1_scstore), .ENDI(graf_1_endi), .RE(cpu_1_re));

  // Notes on the sheet:
  //   CLAVIER
  //   MARCHE / ARRET
  //   ROM GAME CHIP8
  //   ROM (BIOS)
  //   RAM
  //   contents of rom_1 (hex, n*v repeats v):
  //   10 54 10 54 f0 90 90 90 f0 20 60 20 20 70 f0 10 f0 80 f0 f0 10 f0 10 f0 90 90 f0 10 10 f0 80 f0 10
  //   f0 f0 80 f0 90 f0 f0 10 20 40 40 f0 90 f0 90 f0 f0 90 f0 10 f0 f0 90 f0 90 90 e0 90 e0 90 e0 f0 80
  //   80 80 f0 e0 90 90 90 e0 f0 80 f0 80 f0 f0 80 f0 80 80 61 e 62 c 60 0 f0 29 d1 25 71 5 a0 8c d1 25 71
  //   5 a0 91 d1 25 71 5 a0 96 d1 25 71 5 60 a f0 29 d1 25 71 5 a0 9b d1 25 71 5 a0 96 d1 25 63 0 f3 a 0
  //   e0 12 0 0 f0 0 f0 0 70 80 60 10 e0 f0 4*60 e0 90 e0 90 90
  //   CPU
  //   AUDIO
  //   VIDEO
endmodule

module GRAF (
  input  [5:0] AL,
  input  [4:0] AC,
  input  Store,
  input  D,
  input  H,
  input  R,
  input  RE,
  input  M,
  input  E,
  output clear,
  output DIS,
  output Enable,
  output H_2,
  output [4:0] AC_2,
  output [5:0] AL_2,
  output DO,
  output ENDI
);

  wire colc64_2_1_os, igrb_1_igd, igrb_1_ob, igsc_1_ck_i, igsc_1_cl_i, or_1_out;
  wire [4:0] igrb_1_oy;
  wire [5:0] igrb_1_ox;
  wire [11:0] igrb_1_or;
  wire [23:0] rom_1_data;

  or or_1 (or_1_out, R, RE);
  IGSC igsc_1 (
    .DOS(colc64_2_1_os), .AL(AL), .AC(AC), .M(M), .E(E), .D(D), .H(H), .R(or_1_out), .Store(Store), .DO(DO),
    .AL_2(AL_2), .AC_2(AC_2), .clear(clear), .Enable(Enable), .DIS(DIS), .H_2(H_2), .ENDI(ENDI),
    .CL_I(igsc_1_cl_i), .CK_I(igsc_1_ck_i), .AC_I(igrb_1_ox), .AL_I(igrb_1_oy), .D_I(igrb_1_ob),
    .ENDI_I(igrb_1_igd));
  ROM #(.addrWidth(12), .dataWidth(24)) rom_1 (.addr(igrb_1_or), .data(rom_1_data), .sel(1'b1));
  IGRB igrb_1 (
    .I(rom_1_data), .CL(igsc_1_cl_i), .H(igsc_1_ck_i), .OX(igrb_1_ox), .OY(igrb_1_oy), .IGD(igrb_1_igd),
    .OR(igrb_1_or), .OB(igrb_1_ob));
  COLC64_2 colc64_2_1 (.Enable(Enable), .OS(colc64_2_1_os), .X(AL_2), .Y(AC_2), .I(DIS), .H(H_2), .CL(clear));

  // Notes on the sheet:
  //   RE: pull=down
  //   contents of rom_1 (hex, n*v repeats v):
  //   40 20 121*0 6*ffffff 26*0 ffffff 0 0 ffffff 28*0 ffffff 0 0 ffffff 17*0 ffffff ffffff ffffff 8*0
  //   ffffff 0 0 ffffff 16*0 6*ffffff 7*0 ffffff ffffff 16*0 ffffff ffffff 0 0 0 ffffff ffffff ffffff 23*0
  //   ffffff ffffff 6*0 ffffff ffffff 5*0 4*ffffff 12*0 ffffff ffffff 8*0 ffffff ffffff 0 0 0 ffffff 4*0
  //   ffffff 11*0 ffffff 10*0 ffffff 0 0 0 ffffff 4*0 ffffff 11*0 ffffff 10*0 ffffff 0 0 0 ffffff 4*0
  //   ffffff 0 0 6*ffffff 0 0 0 ffffff 10*0 ffffff 4*0 ffffff 0 0 ffffff 8*0 ffffff 0 0 0 ffffff ffffff
  //   ffffff 6*0 ffffff ffffff ffffff 16*0 ffffff 4*0 ffffff ffffff 6*0 ffffff ffffff 4*0 ffffff 12*0
  //   ffffff 18*0 ffffff 12*0 ffffff 0 0 0 ffffff 10*0 ffffff 0 0 0 6*ffffff 11*0 12*ffffff 0 0 0 ffffff
  //   7*0 5*ffffff 4*0 12*ffffff 0 0 0 ffffff 12*0 ffffff 0 0 0 ffffff 4*0 ffffff 5*0 ffffff 16*0 ffffff
  //   8*0 ffffff 9*0 6*ffffff 7*0 ffffff 8*0 ffffff 9*0 ffffff 0 0 ffffff 4*0 5*ffffff 9*0 ffffff 9*0
  //   ffffff 0 0 ffffff 18*0 ffffff 9*0 ffffff 0 0 ffffff ffffff 0 0 0 6*ffffff 0 0 0 ffffff 4*0 ffffff
  //   5*0 ffffff 4*0 ffffff ffffff 0 0 ffffff 0 0 ffffff 4*0 ffffff 0 0 0 12*ffffff 11*0 ffffff 4*0 ffffff
  //   0 0 0 12*ffffff 4*0 4*ffffff 0 0 0 ffffff 4*0 ffffff 0 0 0 ffffff 10*0 ffffff 0 0 0 ffffff 4*0
  //   ffffff 0 0 0 4*ffffff 19*0 ffffff 4*0 ffffff 11*0 ffffff 10*0 ffffff 0 0 0 ffffff 4*0 ffffff 0 0 0
  //   4*ffffff 4*0 12*ffffff 4*0 4*ffffff 0 0 0 ffffff 4*0 ffffff 0 0 0 12*ffffff 11*0 ffffff 4*0 ffffff 0
  //   0 0 ffffff 10*0 ffffff 0 0 0 6*ffffff 0 0 ffffff 4*0 ffffff 18*0 ffffff ffffff 7*0 4*ffffff 4*0
  //   ffffff 10*0 ffffff 5*0 ffffff ffffff 13*0 12*ffffff 7*0 ffffff ffffff 0 0 ffffff ffffff 7*0
  //   12*ffffff 0 0 0 6*ffffff 4*0 ffffff ffffff 5*0 ffffff 4*0 ffffff 5*0 ffffff 15*0 ffffff ffffff 0 0 0
  //   ffffff 4*0 ffffff 9*0 ffffff 4*0 ffffff 4*0 ffffff ffffff 5*0 ffffff 4*0 ffffff 9*0 6*ffffff 0 0
  //   ffffff ffffff 7*0 ffffff ffffff 0 0 ffffff ffffff 9*0 ffffff 4*0 ffffff 12*0 4*ffffff 18*0 ffffff
  //   4*0 ffffff 5*0 ffffff ffffff 12*0 4*ffffff 0 0 0 6*ffffff 18*0 ffffff 4*0 ffffff 0 0 ffffff 4*0
  //   ffffff 8*0 ffffff ffffff 8*0 ffffff 4*0 ffffff 16*0 ffffff ffffff 8*0 ffffff 0 0 0 ffffff ffffff 0 0
  //   0 4*ffffff 9*0 ffffff ffffff 9*0 5*ffffff 0 0 ffffff 4*0 ffffff 8*0 ffffff ffffff 16*0 ffffff 4*0
  //   ffffff 18*0 5*ffffff 0 0 0 ffffff 4*0 ffffff 5*0 ffffff ffffff 0 0 0 ffffff ffffff ffffff 10*0
  //   ffffff 0 0 0 ffffff 0 0 ffffff 5*0 4*ffffff 0 5*ffffff 9*0 ffffff 11*0 ffffff ffffff 0 0 ffffff
  //   ffffff ffffff 0 0 0 ffffff ffffff 8*0 ffffff 11*0 ffffff 4*0 ffffff 5*0 ffffff 0 0 0 5*ffffff 12*0
  //   ffffff 4*0 ffffff 5*0 ffffff 20*0 ffffff ffffff 0 0 ffffff ffffff ffffff 0 0 0 ffffff ffffff 0 0 0
  //   6*ffffff 12*0 4*ffffff 0 5*ffffff 4*0 ffffff 0 0 ffffff 0 ffffff 13*0 ffffff ffffff 0 0 0 ffffff
  //   ffffff ffffff 5*0 ffffff 0 0 ffffff 0 ffffff 26*0 ffffff 0 0 ffffff 0 ffffff 26*0 ffffff 4*0 ffffff
endmodule

module HPBEEP (
  input  in_1,
  output out_2,
  output out_3,
  output out_4
);


  assign out_2 = in_1;
  assign out_3 = in_1;
  assign out_4 = in_1;
endmodule

module keyboard01 (
  input  in_1,
  input  in_2,
  input  in_3,
  input  in_4,
  output [3:0] out_5
);


  assign out_5 = {in_4, in_3, in_2, in_1};
endmodule

module keyboard02 (
  input  [3:0] in_1,
  input  [3:0] in_2,
  input  [3:0] in_3,
  input  [3:0] in_4,
  output [4:0] out_5,
  output out_6
);

  CODH codh_1 (
    .Enable(1'b1), .Validate(out_5[4]), .Output(out_5[3:0]), .Input_0(in_4[1]), .Input_1(in_1[0]),
    .Input_2(in_1[1]), .Input_3(in_1[2]), .Input_4(in_2[0]), .Input_5(in_2[1]), .Input_6(in_2[2]),
    .Input_7(in_3[0]), .Input_8(in_3[1]), .Input_9(in_3[2]), .Input_10(in_4[0]), .Input_11(in_4[2]),
    .Input_12(in_1[3]), .Input_13(in_2[3]), .Input_14(in_3[3]), .Input_15(in_4[3]));  // open: Error

  assign out_6 = out_5[4];
endmodule
